// Logisim project loesungenAufgaben_2.1.circ as structural Verilog: 1 circuit, main circuit main
module main (
  input  A,
  input  A_2,
  input  B,
  input  B_2,
  input  A_3,
  input  B_3,
  input  C,
  input  D,
  input  U,
  input  V,
  input  W,
  input  A_4,
  input  A_5,
  input  B_4,
  input  B_5,
  input  C_2,
  input  C_3
);

  wire and_1_out, and_2_out, and_3_out, and_4_out, nand_1_out, nand_2_out, nor_1_out, not_1_out, not_2_out,
       not_3_out, not_4_out, not_5_out, not_6_out, not_7_out, not_8_out, or_1_out, or_2_out, xor_1_out,
       xor_2_out, xor_3_out, xor_4_out;

  not not_1 (not_1_out, D);
  nand nand_1 (nand_1_out, A, B);
  LED Y (.in(nand_1_out));
  and and_1 (and_1_out, A_3, B_3, C);
  not not_2 (not_2_out, U);
  not not_3 (not_3_out, V);
  not not_4 (not_4_out, U);
  not not_5 (not_5_out, W);
  not not_6 (not_6_out, V);
  xor xor_1 (xor_1_out, B_4, C_2);
  and and_2 (and_2_out, not_2_out, not_3_out, W);
  and and_3 (and_3_out, not_4_out, V, not_5_out);
  and and_4 (and_4_out, U, not_6_out, W);
  xor xor_2 (xor_2_out, A_4, xor_1_out);
  LED Y_2 (.in(xor_2_out));
  nor nor_1 (nor_1_out, and_1_out, not_1_out);
  nand nand_2 (nand_2_out, and_1_out, not_1_out);
  not not_7 (not_7_out, A_2);
  not not_8 (not_8_out, B_2);
  LED Y_3 (.in(nor_1_out));
  LED Z (.in(nand_2_out));
  or or_1 (or_1_out, and_2_out, and_3_out, and_4_out);
  LED Y_4 (.in(or_1_out));
  LED Y_5 (.in(or_2_out));
  or or_2 (or_2_out, not_7_out, not_8_out);
  xor xor_3 (xor_3_out, A_5, B_5);
  xor xor_4 (xor_4_out, xor_3_out, C_3);
  LED Y_6 (.in(xor_4_out));

  // Notes on the sheet:
  //   1.
  //   2.
  //   3.
  //   4.
  //   Aufgaben 2.1
endmodule
