// Logisim project loesungenAufgaben_2.2.circ as structural Verilog: 1 circuit, main circuit main
module main (
  input  X2,
  input  X1,
  input  X0,
  input  X2_2,
  input  X1_2,
  input  X0_2,
  input  X4,
  input  X3,
  input  X2_3,
  input  X1_3,
  input  X0_3,
  input  x2_4,
  input  x1_4,
  input  x0_4,
  input  x2_5,
  input  x1_5,
  input  x0_5
);

  wire and_1_out, and_2_out, and_3_out, and_4_out, and_5_out, and_6_out, and_7_out, and_8_out, and_9_out,
       and_10_out, and_11_out, and_12_out, and_13_out, not_1_out, not_2_out, not_3_out, not_4_out, not_5_out,
       not_6_out, not_7_out, not_8_out, not_9_out, not_10_out, or_1_out, or_2_out, or_3_out, or_4_out,
       or_5_out, or_6_out, or_7_out, or_8_out, or_9_out, undriven, undriven_2, undriven_3, undriven_4;

  LED led_1 (.in(undriven));
  LED led_2 (.in(undriven));
  LED led_3 (.in(undriven));
  not not_1 (not_1_out, x1_4);
  not not_2 (not_2_out, x1_5);
  not not_3 (not_3_out, X2);
  not not_4 (not_4_out, X0);
  not not_5 (not_5_out, X0);
  not not_6 (not_6_out, X0_2);
  LED led_4 (.in(undriven_2));
  LED led_5 (.in(undriven_2));
  LED led_6 (.in(undriven_2));
  LED led_7 (.in(undriven_4));
  LED led_8 (.in(undriven_3));
  LED led_9 (.in(undriven_3));
  LED led_10 (.in(undriven_3));
  not not_7 (not_7_out, x0_4);
  not not_8 (not_8_out, x0_5);
  and and_1 (and_1_out, not_3_out, X1, not_4_out);
  and and_2 (and_2_out, X2, X1, not_5_out);
  and and_3 (and_3_out, X2, X1, X0);
  and and_4 (and_4_out, X1_2, not_6_out);
  and and_5 (and_5_out, X2_2, X1_2);
  not not_9 (not_9_out, X1_3);
  not not_10 (not_10_out, X2_3);
  LED led_11 (.in(undriven_4));
  LED led_12 (.in(undriven_4));
  and and_6 (and_6_out, x1_4, not_7_out);
  and and_7 (and_7_out, not_1_out, x0_4);
  or or_1 (or_1_out, x2_5, x0_5);
  or or_2 (or_2_out, x2_5, x1_5);
  or or_3 (or_3_out, and_4_out, and_5_out);
  and and_8 (and_8_out, not_9_out, X0_3);
  and and_9 (and_9_out, not_10_out, X0_3);
  and and_10 (and_10_out, X3, X0_3);
  and and_11 (and_11_out, X4, X0_3);
  or or_4 (or_4_out, and_1_out, and_2_out, and_3_out);
  LED Y (.in(or_4_out));
  LED Y_2 (.in(or_3_out));
  or or_5 (or_5_out, and_8_out, and_9_out, and_10_out, and_11_out);
  or or_6 (or_6_out, x2_4, x0_4);
  or or_7 (or_7_out, and_6_out, x2_4);
  or or_8 (or_8_out, and_7_out, x2_4);
  or or_9 (or_9_out, x2_4, x1_4);
  and and_12 (and_12_out, or_2_out, not_8_out);
  and and_13 (and_13_out, or_1_out, not_2_out);
  LED Y_3 (.in(or_5_out));
  LED led_13 (.in(or_9_out));
  LED led_14 (.in(or_9_out));
  LED led_15 (.in(or_2_out));
  LED led_16 (.in(or_2_out));
  LED led_17 (.in(or_6_out));
  LED led_18 (.in(or_6_out));
  LED led_19 (.in(or_6_out));
  LED led_20 (.in(or_9_out));
  LED led_21 (.in(or_8_out));
  LED led_22 (.in(or_8_out));
  LED led_23 (.in(or_8_out));
  LED led_24 (.in(or_1_out));
  LED led_25 (.in(or_1_out));
  LED led_26 (.in(or_1_out));
  LED led_27 (.in(or_2_out));
  LED led_28 (.in(and_13_out));
  LED led_29 (.in(and_13_out));
  LED led_30 (.in(and_13_out));
  LED led_31 (.in(or_7_out));
  LED led_32 (.in(or_7_out));
  LED led_33 (.in(and_12_out));
  LED led_34 (.in(and_12_out));
  LED led_35 (.in(or_7_out));
  LED led_36 (.in(and_12_out));

  // Notes on the sheet:
  //   1a.
  //   1c.
  //   2.
  //   3.
  //   Aufgaben 2.2
  //   a
  //   b
  //   c
  //   d
  //   a
  //   b
  //   d
  //   c
endmodule
