// Logisim project loesungenSkriptSchaltalgebra.circ as structural Verilog: 15 circuits, main circuit Aufgabe Seite 2
module Aufgabe_Seite_2 (
  input  in_1,
  input  in_2,
  input  in_3,
  input  in_4,
  input  x0,
  input  x1,
  input  [3:0] \function ,
  output out_8,
  output out_9,
  output out_10,
  output out_11,
  output y
);

  Kontradiktion kontradiktion_1 (.x(in_1), .y(out_8));
  \Identität  \identität_1  (.x(in_2), .y(out_9));
  Negation negation_1 (.x(in_3), .y(out_10));
  Tautologie tautologie_1 (.x(in_4), .y(out_11));
  Selectable_2_Input_Function selectable_2_input_function_1 (.x0(x0), .x1(x1), .\function (\function ), .y(y));

  // Notes on the sheet:
  //   Aufgabe Seite 2
  //   Hinweis: Mit 2 Eingangsvariablen sind
  //   insgesamt 16 unterschiedliche Wahrheitstabellen möglich
  //   Kontradiktion   (nie)
  //   Identität   (gleich)
  //   Negation   (nicht)
  //   Tautologie   (immer)
endmodule

module Fragen_Seite_4 (
  input  x0,
  input  x0_2,
  input  x1,
  input  x1_2,
  input  x0_3,
  input  x0_4,
  input  x1_3,
  input  x1_4,
  input  x0_5,
  input  x0_6,
  input  x1_5,
  input  x1_6,
  output y,
  output y_2,
  output y_3,
  output y_4,
  output y_5,
  output y_6
);

  Selectable_2_Input_Function selectable_2_input_function_1 (.x0(x0), .x1(x1), .\function (4'b0001), .y(y));
  Selectable_2_Input_Function selectable_2_input_function_2 (.x0(x0_3), .x1(x1_3), .\function (4'b0111), .y(y_3));
  Selectable_2_Input_Function selectable_2_input_function_3 (.x0(x0_5), .x1(x1_5), .\function (4'b0110), .y(y_5));
  Selectable_2_Input_Function selectable_2_input_function_4 (.x0(x0_2), .x1(x1_2), .\function (4'b1110), .y(y_2));
  Selectable_2_Input_Function selectable_2_input_function_5 (.x0(x0_4), .x1(x1_4), .\function (4'b1000), .y(y_4));
  Selectable_2_Input_Function selectable_2_input_function_6 (.x0(x0_6), .x1(x1_6), .\function (4'b1001), .y(y_6));

  // Notes on the sheet:
  //   Fragen Seite 4
  //   AND
  //   OR
  //   EXOR
  //   NAND
  //   NOR
  //   EXNOR
endmodule

module Frage_Seite_5 (
  input  x1,
  input  x1_2,
  input  x0,
  input  x0_2
);

  wire nor_1_out, not_1_out, or_1_out;

  // Probe on nor_1_out
  nor nor_1 (nor_1_out, x1, x0);
  or or_1 (or_1_out, x1_2, x0_2);
  not not_1 (not_1_out, or_1_out);
  // Probe on not_1_out

  // Notes on the sheet:
  //   Frage Seite 5
  //    NOR
  //   y = x1 + x0
  //   ______
endmodule

module Frage_Seite_6 (
  input  x1,
  input  x0,
  output y
);

  wire and_1_out, and_2_out, not_1_out, not_2_out;

  not not_1 (not_1_out, x1);
  not not_2 (not_2_out, x0);
  and and_1 (and_1_out, not_1_out, x0);
  and and_2 (and_2_out, x1, not_2_out);
  or or_1 (y, and_1_out, and_2_out);

  // Notes on the sheet:
  //   Fragen Seite 6
endmodule

module Aufgabe_Seite_8 (
  input  A,
  input  B,
  input  B_2,
  input  C,
  input  C_2,
  input  A_2,
  input  D,
  output y,
  output y_2
);

  wire and_1_out, and_2_out, or_2_out;

  and and_1 (and_1_out, A, B_2);
  and and_2 (and_2_out, C_2, D);
  or or_1 (y_2, and_1_out, and_2_out);
  or or_2 (or_2_out, B, C);
  and and_3 (y, or_2_out, A_2);

  // Notes on the sheet:
  //   Aufgabe Seite 8
endmodule

module Aufgabe_Seite_8_Forts (
  input  A,
  input  B,
  input  B_2,
  input  C,
  input  C_2,
  input  A_2,
  output y,
  output y_2
);

  wire and_1_out, nor_1_out;

  and and_1 (and_1_out, A, B_2);
  or or_1 (y_2, and_1_out, C_2);
  nor nor_1 (nor_1_out, B, C);
  and and_2 (y, nor_1_out, A_2);

  // Notes on the sheet:
  //   Aufgabe Seite 8 Forts.
endmodule

module Aufgabe_Seite_8_Forts__2 (
  input  A,
  input  B,
  input  C,
  output y
);

  wire and_1_out;

  and and_1 (and_1_out, B, C);
  or or_1 (y, A, and_1_out);

  // Notes on the sheet:
  //   Aufgabe Seite 8 Forts. 2
endmodule

module Aufgabe_Seite_8_Forts__3 (
  input  A,
  input  B,
  input  C,
  input  D,
  input  E,
  output y
);

  wire and_1_out, nand_1_out;

  and and_1 (and_1_out, A, ~B);  // AND_Gate
  nand nand_1 (nand_1_out, C, D, E);
  or or_1 (y, and_1_out, nand_1_out);

  // Notes on the sheet:
  //   Aufgabe Seite 8 Forts. 3
endmodule

module Aufgabe_Seite_8_Forts__4 (
  input  A,
  input  B,
  input  C,
  input  D,
  input  E,
  output y
);

  wire and_1_out, nand_1_out;

  and and_1 (and_1_out, A, ~B);  // AND_Gate
  nand nand_1 (nand_1_out, C, D, E);
  nor nor_1 (y, and_1_out, nand_1_out);

  // Notes on the sheet:
  //   Aufgabe Seite 8 Forts. 4
endmodule

module Aufgaben_Seite_13 (
  input  A,
  input  C,
  input  D,
  input  B,
  input  A_2,
  input  C_2,
  input  B_2,
  input  D_2,
  input  A_3,
  input  C_3,
  input  D_3,
  input  B_3,
  input  A_4,
  input  C_4,
  input  D_4,
  input  B_4,
  output y___ACD___BD,
  output y___ACD___BD___D_AC___B,
  output y___ACD_BD,
  output y___ACD_BD_2
);

  wire and_1_out, and_2_out, and_3_out, nand_1_out, nand_2_out, nand_3_out, nand_4_out, nor_1_out, nor_2_out,
       nor_3_out, nor_4_out, nor_5_out, nor_6_out, nor_7_out, nor_8_out, nor_9_out, or_2_out;

  and and_1 (and_1_out, A, C, D);
  and and_2 (and_2_out, D, B);
  and and_3 (and_3_out, A_2, C_2);
  nor nor_1 (nor_1_out, A_3, 1'b0);
  nor nor_2 (nor_2_out, C_3, 1'b0);
  nor nor_3 (nor_3_out, D_3, 1'b0);
  nor nor_4 (nor_4_out, B_3, 1'b0);
  nand nand_1 (nand_1_out, A_4, C_4);
  or or_1 (y___ACD___BD, and_1_out, and_2_out);
  or or_2 (or_2_out, and_3_out, B_2);
  nor nor_5 (nor_5_out, nor_1_out, nor_2_out);
  nor nor_6 (nor_6_out, nor_3_out, nor_4_out);
  nand nand_2 (nand_2_out, 1'b1, nand_1_out);
  nand nand_3 (nand_3_out, D_4, B_4);
  and and_4 (y___ACD___BD___D_AC___B, or_2_out, D_2);
  nor nor_7 (nor_7_out, nor_5_out, 1'b0);
  nand nand_4 (nand_4_out, nand_2_out, D_4);
  nor nor_8 (nor_8_out, nor_7_out, nor_3_out);
  nand nand_5 (y___ACD_BD_2, nand_4_out, nand_3_out);
  nor nor_9 (nor_9_out, nor_8_out, nor_6_out);
  nor nor_10 (y___ACD_BD, nor_9_out, 1'b0);

  // Notes on the sheet:
  //   Aufgaben Seite 13
  //   Lösung mit 2-Input-NOR
endmodule

module Kontradiktion (
  input  x,
  output y
);


  assign y = 1'b0;
endmodule

module \Identität  (
  input  x,
  output y
);


  assign y = x;
endmodule

module Tautologie (
  input  x,
  output y
);


  assign y = 1'b1;
endmodule

module Negation (
  input  x,
  output y
);

  not not_1 (y, x);
endmodule

module Selectable_2_Input_Function (
  input  x0,
  input  x1,
  input  [3:0] \function ,
  output y
);

  ROM #(.addrWidth(6), .dataWidth(1)) rom_1 (.addr({\function , x1, x0}), .data(y));  // open: sel

  // Notes on the sheet:
  //   contents of rom_1 (hex, n*v repeats v):
  //   7*0 1 0 0 1 0 0 0 1 1 0 1 0 0 0 1 0 1 0 1 1 0 0 4*1 0 0 0 1 0 0 1 1 0 1 0 1 0 4*1 0 0 1 1 0 4*1 0
  //   4*1
endmodule
