// Logisim project schaltalgebra.circ as structural Verilog: 15 circuits, main circuit Seite 02
module Seite_02 (
  input  x,
  input  x_2
);

  wire buffer_1_out, not_1_out;

  buf buffer_1 (buffer_1_out, x);
  // Probe on buffer_1_out
  not not_1 (not_1_out, x_2);
  // Probe on not_1_out

  // Notes on the sheet:
  //   Puffer
  //   y = x
  //   Inverter
  //   _
  //   y = x
endmodule

module Seite_03 (
  input  x1,
  input  x0
);

  wire and_1_out;

  // Probe on and_1_out
  and and_1 (and_1_out, x1, x0);

  // Notes on the sheet:
  //   AND-Gatter
  //   y = x1 * x0
endmodule

module Seite_04 (
  input  x1,
  input  x0
);

  wire or_1_out;

  or or_1 (or_1_out, x1, x0);
  // Probe on or_1_out

  // Notes on the sheet:
  //   OR-Gatter
  //   y = x1 + x0
endmodule

module Seite_05 (
  input  x1,
  input  x1_2,
  input  x0,
  input  x0_2,
  input  x1_3,
  input  x1_4,
  input  x0_3,
  input  x0_4
);

  wire and_1_out, nand_1_out, nor_1_out, not_1_out, not_2_out, or_1_out;

  // Probe on nand_1_out
  nand nand_1 (nand_1_out, x1, x0);
  // Probe on nor_1_out
  nor nor_1 (nor_1_out, x1_3, x0_3);
  and and_1 (and_1_out, x1_2, x0_2);
  or or_1 (or_1_out, x1_4, x0_4);
  not not_1 (not_1_out, and_1_out);
  // Probe on not_1_out
  not not_2 (not_2_out, or_1_out);
  // Probe on not_2_out

  // Notes on the sheet:
  //   NAND
  //   ______
  //   y = x1 * x0
  //    NOR
  //   ______
  //   y = x1 + x0
endmodule

module Seite_06a (
  input  x1,
  input  x0,
  input  x1_2,
  input  x0_2
);

  wire and_1_out, and_2_out, or_1_out, xor_1_out;

  // Probe on xor_1_out
  xor xor_1 (xor_1_out, x1, x0);
  and and_1 (and_1_out, x1_2, ~x0_2);  // AND_Gate
  and and_2 (and_2_out, ~x1_2, x0_2);  // AND_Gate
  or or_1 (or_1_out, and_1_out, and_2_out);
  // Probe on or_1_out

  // Notes on the sheet:
  //   EXOR  (Antivalenz)
  //   y = x1 + x0
  //   O
endmodule

module Seite_06b (
  input  x1,
  input  x0,
  input  x1_2,
  input  x0_2
);

  wire and_1_out, and_2_out, or_1_out, xnor_1_out;

  xnor xnor_1 (xnor_1_out, x1, x0);
  // Probe on xnor_1_out
  and and_1 (and_1_out, x1_2, x0_2);
  and and_2 (and_2_out, ~x1_2, ~x0_2);  // AND_Gate
  or or_1 (or_1_out, and_1_out, and_2_out);
  // Probe on or_1_out

  // Notes on the sheet:
  //   EXNOR  (Aequivalenz)
  //   ______
  //   O
  //   y = x1 + x0
endmodule

module Seite_09a (
  input  A,
  input  B,
  input  C,
  input  A_2,
  input  B_2,
  input  C_2,
  input  A_3,
  input  B_3,
  input  C_3
);

  wire and_1_out, and_2_out, and_3_out, and_4_out, and_5_out;

  and and_1 (and_1_out, B, C);
  and and_2 (and_2_out, A_2, B_2);
  and and_3 (and_3_out, A, and_1_out);
  // Probe on and_3_out
  and and_4 (and_4_out, and_2_out, C_2);
  // Probe on and_4_out
  and and_5 (and_5_out, A_3, B_3, C_3);
  // Probe on and_5_out

  // Notes on the sheet:
  //   Assoziative Gesetze
endmodule

module Seite_09b (
  input  A,
  input  B,
  input  C,
  input  A_2,
  input  B_2,
  input  C_2,
  input  A_3,
  input  B_3,
  input  C_3
);

  wire or_1_out, or_2_out, or_3_out, or_4_out, or_5_out;

  or or_1 (or_1_out, B, C);
  or or_2 (or_2_out, A_2, B_2);
  // Probe on or_3_out
  or or_3 (or_3_out, A, or_1_out);
  // Probe on or_4_out
  or or_4 (or_4_out, or_2_out, C_2);
  or or_5 (or_5_out, A_3, B_3, C_3);
  // Probe on or_5_out

  // Notes on the sheet:
  //   Assoziative Gesetze
endmodule

module Seite_09c (
  input  A,
  input  B,
  input  C,
  input  A_2,
  input  B_2,
  input  C_2
);

  wire and_1_out, and_2_out, and_3_out, or_1_out, or_2_out;

  or or_1 (or_1_out, B, C);
  and and_1 (and_1_out, A_2, B_2);
  and and_2 (and_2_out, A_2, C_2);
  and and_3 (and_3_out, A, or_1_out);
  or or_2 (or_2_out, and_1_out, and_2_out);
  // Probe on and_3_out
  // Probe on or_2_out

  // Notes on the sheet:
  //   Distributive Gesetze
endmodule

module Seite_09d (
  input  A,
  input  B,
  input  C,
  input  A_2,
  input  B_2,
  input  C_2
);

  wire and_1_out, and_2_out, or_1_out, or_2_out, or_3_out;

  and and_1 (and_1_out, B, C);
  or or_1 (or_1_out, A_2, B_2);
  or or_2 (or_2_out, A_2, C_2);
  or or_3 (or_3_out, A, and_1_out);
  and and_2 (and_2_out, or_1_out, or_2_out);
  // Probe on or_3_out
  // Probe on and_2_out

  // Notes on the sheet:
  //   Distributive Gesetze
endmodule

module Seite_09e (
  input  A,
  input  A_2,
  input  B,
  input  B_2,
  input  A_3,
  input  A_4,
  input  B_3,
  input  B_4
);

  wire and_1_out, nand_1_out, nor_1_out, or_1_out;

  // Probe on nand_1_out
  nand nand_1 (nand_1_out, A, B);
  // Probe on nor_1_out
  nor nor_1 (nor_1_out, A_3, B_3);
  or or_1 (or_1_out, ~A_2, ~B_2);  // OR_Gate
  // Probe on or_1_out
  and and_1 (and_1_out, ~A_4, ~B_4);  // AND_Gate
  // Probe on and_1_out

  // Notes on the sheet:
  //   De Morgan
  //   De Morgan
endmodule

module Seite_09f (
  input  A,
  input  A_2,
  input  A_3,
  input  A_4,
  input  A_5,
  input  A_6,
  input  A_7,
  input  B,
  input  A_8,
  input  B_2
);

  wire and_1_out, and_2_out, or_1_out, or_2_out, or_3_out, or_4_out, or_5_out, or_6_out, or_7_out, or_8_out;

  // Probe on or_1_out
  or or_1 (or_1_out, A, 1'b0);
  or or_2 (or_2_out, A_3, A_3);
  // Probe on or_2_out
  // Probe on or_3_out
  or or_3 (or_3_out, A_4, ~A_4);  // OR_Gate
  or or_4 (or_4_out, A_5, 1'b1);
  // Probe on or_4_out
  and and_1 (and_1_out, A_7, B);
  and and_2 (and_2_out, ~A_8, B_2);  // AND_Gate
  // Probe on or_5_out
  or or_5 (or_5_out, A_7, and_1_out);
  // Probe on or_6_out
  or or_6 (or_6_out, A_8, and_2_out);
  or or_7 (or_7_out, A_2, 1'b0);
  or or_8 (or_8_out, A_6, 1'b1);
  // Probe on or_7_out
  // Probe on or_8_out

  // Notes on the sheet:
  //   Logische Summen
endmodule

module Seite_09g (
  input  A,
  input  A_2,
  input  A_3,
  input  A_4,
  input  A_5,
  input  A_6,
  input  A_7,
  input  B,
  input  A_8,
  input  B_2
);

  wire and_1_out, and_2_out, and_3_out, and_4_out, and_5_out, and_6_out, and_7_out, and_8_out, or_1_out,
       or_2_out;

  and and_1 (and_1_out, A, 1'b0);
  // Probe on and_1_out
  // Probe on and_2_out
  and and_2 (and_2_out, A_3, A_3);
  and and_3 (and_3_out, A_4, ~A_4);  // AND_Gate
  // Probe on and_3_out
  and and_4 (and_4_out, A_5, 1'b1);
  // Probe on and_4_out
  or or_1 (or_1_out, A_7, B);
  or or_2 (or_2_out, ~A_8, B_2);  // OR_Gate
  // Probe on and_5_out
  and and_5 (and_5_out, A_7, or_1_out);
  // Probe on and_6_out
  and and_6 (and_6_out, A_8, or_2_out);
  and and_7 (and_7_out, A_2, 1'b0);
  and and_8 (and_8_out, A_6, 1'b1);
  // Probe on and_7_out
  // Probe on and_8_out

  // Notes on the sheet:
  //   Logische Produkte
endmodule

module Seite_09h (
  input  A,
  input  B,
  input  C,
  input  A_2,
  input  B_2,
  input  C_2
);

  wire and_1_out, nand_1_out, not_1_out, or_1_out, or_2_out;

  not not_1 (not_1_out, A);
  and and_1 (and_1_out, B, C);
  or or_1 (or_1_out, ~B_2, ~C_2);  // OR_Gate
  or or_2 (or_2_out, not_1_out, and_1_out, 1'b0);
  nand nand_1 (nand_1_out, A_2, or_1_out, 1'b1);
  // Probe on or_2_out
  // Probe on nand_1_out

  // Notes on the sheet:
  //   Beispiel zum Satz von Shannon
endmodule

module Seite_12 (
  input  A,
  input  B,
  input  C
);

  wire and_1_out, and_2_out, not_1_out, or_1_out;

  and and_1 (and_1_out, A, B);
  not not_1 (not_1_out, A);
  and and_2 (and_2_out, not_1_out, C);
  // Probe on or_1_out
  or or_1 (or_1_out, and_1_out, and_2_out);

  // Notes on the sheet:
  //   Fragestellung
endmodule
