// Logisim project adderSubtractor.circ as structural Verilog
module HA__Black_Box (
  input  a,
  input  b,
  output c,
  output s
);

  HA ha_1 (.a(a), .b(b), .c(c), .s(s));

  // Notes on the sheet:
  //   Halbaddierer (Half Adder) in Black Box Darstellung
endmodule

module HA (
  input  a,
  input  b,
  output c,
  output s
);

  and and_1 (c, b, a);
  xor xor_1 (s, a, b);

  // Notes on the sheet:
  //   Halbaddierer
endmodule

module VA__Black_Box (
  input  a,
  input  b,
  input  cin,
  output cout,
  output s
);

  VA_mit_HA_realisiert va_mit_ha_realisiert_1 (.a(a), .b(b), .cin(cin), .cout(cout), .s(s));

  // Notes on the sheet:
  //   Volladdierer
endmodule

module VA_mit_HA (
  input  a,
  input  b,
  input  cin,
  output cout,
  output s
);

  wire ha_1_c, ha_1_s, ha_2_c;

  HA ha_1 (.a(a), .b(b), .c(ha_1_c), .s(ha_1_s));
  HA ha_2 (.a(ha_1_s), .b(cin), .c(ha_2_c), .s(s));
  form form_1 ();

  // Notes on the sheet:
  //   Volladdierer (Full Adder) mit HA realisierbar?
  //   s'
  //   c'
  //   c
endmodule

module VA_mit_HA_realisiert (
  input  a,
  input  b,
  input  cin,
  output cout,
  output s
);

  wire ha_1_c, ha_1_s, ha_2_c;

  HA ha_1 (.a(a), .b(b), .c(ha_1_c), .s(ha_1_s));
  HA ha_2 (.a(ha_1_s), .b(cin), .c(ha_2_c), .s(s));
  or or_1 (cout, ha_1_c, ha_2_c);

  // Notes on the sheet:
  //   Volladdierer mit HA realisiert
endmodule

module RCA (
  input  cin0,
  input  b0,
  input  a0,
  input  b1,
  input  a1,
  input  b2,
  input  a2,
  input  b3,
  input  a3,
  output s0,
  output s1,
  output s2,
  output s3,
  output cout3
);

  wire va_mit_ha_realisiert_1_cout, va_mit_ha_realisiert_2_cout, va_mit_ha_realisiert_3_cout;

  VA_mit_HA_realisiert va_mit_ha_realisiert_1 (.a(a0), .b(b0), .cin(cin0), .cout(va_mit_ha_realisiert_1_cout), .s(s0));
  VA_mit_HA_realisiert va_mit_ha_realisiert_2 (
    .a(a1), .b(b1), .cin(va_mit_ha_realisiert_1_cout), .cout(va_mit_ha_realisiert_2_cout), .s(s1));
  VA_mit_HA_realisiert va_mit_ha_realisiert_3 (
    .a(a2), .b(b2), .cin(va_mit_ha_realisiert_2_cout), .cout(va_mit_ha_realisiert_3_cout), .s(s2));
  VA_mit_HA_realisiert va_mit_ha_realisiert_4 (.a(a3), .b(b3), .cin(va_mit_ha_realisiert_3_cout), .cout(cout3), .s(s3));

  // Notes on the sheet:
  //   Ripple Carry Adder (RCA) mit VA realisiert
  //   cout0
  //   cin1
  //   cout1
  //   cin2
  //   cout2
  //   cin3
endmodule

module HS__Black_Box (
  input  m,
  input  s,
  output b,
  output d
);

  HS hs_1 (.m(m), .s(s), .b(b), .d(d));

  // Notes on the sheet:
  //   Halbsubtrahierer (Half Subtractor) in Black Box Darstellung
  //   m: minuend
  //   s: subtrahend
  //   d: difference
  //   b: borrow
endmodule

module HS (
  input  m,
  input  s,
  output b,
  output d
);

  and and_1 (b, s, ~m);  // AND_Gate
  xor xor_1 (d, m, s);

  // Notes on the sheet:
  //   Halbsubtrahierer (m - s)
  //   m: minuend
  //   s: subtrahend
  //   d: difference
  //   b: borrow
endmodule

module VS__Black_Box (
  input  s,
  input  m,
  input  bin,
  output bout,
  output d
);

  VS_mit_HS_realisiert vs_mit_hs_realisiert_1 (.m(m), .s(s), .bout(bout), .bin(bin), .d(d));

  // Notes on the sheet:
  //   Vollsubtrahierer (m - s - bin)
  //   m: minuend
  //   s: subtrahend
  //   bin: borrow in
  //   d: difference
  //   bout: borrow out
endmodule

module VS_mi_HS (
  input  m,
  input  s,
  input  bin,
  output bout,
  output d
);

  wire hs_1_b, hs_1_d, hs_2_b;

  HS hs_1 (.m(m), .s(s), .b(hs_1_b), .d(hs_1_d));
  HS hs_2 (.m(hs_1_d), .s(bin), .b(hs_2_b), .d(d));
  form form_1 ();

  // Notes on the sheet:
  //   Vollsubtrahierer (Full Subtractor) mit HS realisierbar?
  //   d'
  //   b'
  //   b
endmodule

module VS_mit_HS_realisiert (
  input  m,
  input  s,
  input  bin,
  output bout,
  output d
);

  wire hs_1_b, hs_1_d, hs_2_b;

  HS hs_1 (.m(m), .s(s), .b(hs_1_b), .d(hs_1_d));
  HS hs_2 (.m(hs_1_d), .s(bin), .b(hs_2_b), .d(d));
  or or_1 (bout, hs_1_b, hs_2_b);

  // Notes on the sheet:
  //   Vollsubtrahierer mit HS realisiert
endmodule

module RBS (
  input  bin0,
  input  m0,
  input  s0,
  input  m1,
  input  s1,
  input  m2,
  input  s2,
  input  m3,
  input  s3,
  output d0,
  output d1,
  output d2,
  output d3,
  output bout3
);

  wire vs_mit_hs_realisiert_1_bout, vs_mit_hs_realisiert_2_bout, vs_mit_hs_realisiert_3_bout;

  VS_mit_HS_realisiert vs_mit_hs_realisiert_1 (.m(m0), .s(s0), .bout(vs_mit_hs_realisiert_1_bout), .bin(bin0), .d(d0));
  VS_mit_HS_realisiert vs_mit_hs_realisiert_2 (
    .m(m1), .s(s1), .bout(vs_mit_hs_realisiert_2_bout), .bin(vs_mit_hs_realisiert_1_bout), .d(d1));
  VS_mit_HS_realisiert vs_mit_hs_realisiert_3 (
    .m(m2), .s(s2), .bout(vs_mit_hs_realisiert_3_bout), .bin(vs_mit_hs_realisiert_2_bout), .d(d2));
  VS_mit_HS_realisiert vs_mit_hs_realisiert_4 (.m(m3), .s(s3), .bout(bout3), .bin(vs_mit_hs_realisiert_3_bout), .d(d3));

  // Notes on the sheet:
  //   Ripple Borrow Subtractor (RBS) mit VS realisiert (m - s)
  //   bout0
  //   bin1
  //   bout1
  //   bin2
  //   bout2
  //   bin3
  //   m: minuend
  //   s: subtrahend
  //   d: difference
  //   b: borrow
endmodule
