// Logisim project plexers.circ as structural Verilog: 5 circuits, main circuit Multiplexer aus der Bibliothek
module Multiplexer_aus_der_Bibliothek (
  input  A,
  input  A_2,
  input  A_3,
  input  B,
  input  B_2,
  input  B_3,
  input  S,
  input  S_2,
  input  Enable,
  input  S_3,
  input  Enable_2,
  input  A_4,
  input  A_5,
  input  B_4,
  input  B_5,
  input  C,
  input  C_2,
  input  D,
  input  D_2,
  input  [1:0] S_4,
  input  [1:0] S_5,
  input  Enable_3,
  input  A_6,
  input  B_6,
  input  C_3,
  input  D_3,
  input  E,
  input  [7:0] X,
  input  F,
  input  G,
  input  H,
  input  [2:0] S_6,
  input  Enable_4,
  input  [2:0] S_7,
  input  Enable_5,
  output Y,
  output Y_2,
  output nY,
  output Y_3,
  output Y_4,
  output Y_5,
  output Y_6
);

  wire multiplexer_6_out;

  Multiplexer #(.enable("false")) multiplexer_1 (.in0(A), .in1(B), .out(Y), .sel(S));
  Multiplexer #(.select(2), .enable("false")) multiplexer_2 (
    .in0(A_4), .in1(B_4), .in2(C), .in3(D), .out(Y_3), .sel(S_4));
  Multiplexer #(.disabled(0)) multiplexer_3 (.in0(A_2), .in1(B_2), .out(Y_2), .sel(S_2), .en(Enable));
  Multiplexer #(.select(2), .disabled(0)) multiplexer_4 (
    .in0(A_5), .in1(B_5), .in2(C_2), .in3(D_2), .out(Y_4), .sel(S_5), .en(Enable_3));
  Multiplexer #(.select(3), .disabled(0)) multiplexer_5 (
    .in0(A_6), .in1(B_6), .in2(C_3), .in3(D_3), .in4(E), .in5(F), .in6(G), .in7(H), .out(Y_5), .sel(S_6),
    .en(Enable_4));
  not not_1 (nY, multiplexer_6_out);
  Multiplexer #(.disabled(0)) multiplexer_6 (.in0(A_3), .in1(B_3), .out(multiplexer_6_out), .sel(S_3), .en(Enable_2));
  Multiplexer #(.select(3), .disabled(0)) multiplexer_7 (
    .in0(X[0]), .in1(X[1]), .in2(X[2]), .in3(X[3]), .in4(X[4]), .in5(X[5]), .in6(X[6]), .in7(X[7]),
    .out(Y_6), .sel(S_7), .en(Enable_5));

  // Notes on the sheet:
  //   Multiplexer aus der Bibliothek
  //   MUX 2:1
  //   MUX 4:1
  //   MUX 2:1 mit Enable
  //   MUX 4:1 mit Enable
  //   MUX 8:1 mit Enable
  //   MUX 2:1 mit Enable, logisch negativer Ausgang
  //   H G F  E D C B A
  //   MUX 8:1 mit Enable, gebündelte Eingänge X und S
endmodule

module Mehrfach_MUXes__parallel (
  input  [2:0] S,
  input  Enable,
  input  A0,
  input  B0,
  input  C0,
  input  D0,
  input  E0,
  input  F0,
  input  G0,
  input  H0,
  input  A1,
  input  B1,
  input  C1,
  input  D1,
  input  E1,
  input  F1,
  input  G1,
  input  H1,
  input  [3:0] A,
  input  [3:0] B,
  input  [3:0] C,
  input  [3:0] D,
  input  [3:0] E,
  input  [3:0] F,
  input  A2,
  input  [3:0] G,
  input  B2,
  input  [3:0] H,
  input  C2,
  input  D2,
  input  E2,
  input  F2,
  input  [2:0] S_2,
  input  Enable_2,
  input  G2,
  input  H2,
  input  A3,
  input  B3,
  input  C3,
  input  D3,
  input  E3,
  input  F3,
  input  G3,
  input  H3,
  output [3:0] Y,
  output [3:0] Y_2
);

  Multiplexer #(.select(3), .disabled(0)) multiplexer_1 (
    .in0(A0), .in1(B0), .in2(C0), .in3(D0), .in4(E0), .in5(F0), .in6(G0), .in7(H0), .out(Y[0]), .sel(S),
    .en(Enable));
  Multiplexer #(.select(3), .disabled(0)) multiplexer_2 (
    .in0(A1), .in1(B1), .in2(C1), .in3(D1), .in4(E1), .in5(F1), .in6(G1), .in7(H1), .out(Y[1]), .sel(S),
    .en(Enable));
  Multiplexer #(.select(3), .disabled(0)) multiplexer_3 (
    .in0(A2), .in1(B2), .in2(C2), .in3(D2), .in4(E2), .in5(F2), .in6(G2), .in7(H2), .out(Y[2]), .sel(S),
    .en(Enable));
  Multiplexer #(.select(3), .disabled(0)) multiplexer_4 (
    .in0(A3), .in1(B3), .in2(C3), .in3(D3), .in4(E3), .in5(F3), .in6(G3), .in7(H3), .out(Y[3]), .sel(S),
    .en(Enable));
  Multiplexer #(.select(3), .width(4), .disabled(0)) multiplexer_5 (
    .in0(A), .in1(B), .in2(C), .in3(D), .in4(E), .in5(F), .in6(G), .in7(H), .out(Y_2), .sel(S_2),
    .en(Enable_2));

  // Notes on the sheet:
  //   Mehrere parallele Multiplexer
  //   ungebündelte Eingänge (1-Bit Eingänge)
  //   =
  //   MUX 8:1 mit 4-Bit Eingängen (je 4 Bit gebündelt)
endmodule

module Demultiplexer_aus_der_Bibliothek (
  input  X,
  input  X_2,
  input  S,
  input  S_2,
  input  Enable,
  input  X_3,
  input  X_4,
  input  [1:0] S_3,
  input  [1:0] S_4,
  input  Enable_2,
  input  X_5,
  input  X_6,
  input  [2:0] S_5,
  input  Enable_3,
  input  [2:0] S_6,
  input  Enable_4,
  output P,
  output P_2,
  output Q,
  output Q_2,
  output P_3,
  output P_4,
  output Q_3,
  output Q_4,
  output R,
  output R_2,
  output S_7,
  output S_8,
  output P_5,
  output Q_5,
  output R_3,
  output S_9,
  output [7:0] X_7,
  output T,
  output U,
  output V,
  output W
);

  Demultiplexer #(.disabled(0), .enable("false")) demultiplexer_1 (.out0(P), .out1(Q), .in(X), .sel(S));
  Demultiplexer #(.select(2), .disabled(0), .enable("false")) demultiplexer_2 (
    .out0(P_3), .out1(Q_3), .out2(R), .out3(S_7), .in(X_3), .sel(S_3));
  Demultiplexer #(.disabled(0)) demultiplexer_3 (.out0(P_2), .out1(Q_2), .in(X_2), .sel(S_2), .en(Enable));
  Demultiplexer #(.select(2), .disabled(0)) demultiplexer_4 (
    .out0(P_4), .out1(Q_4), .out2(R_2), .out3(S_8), .in(X_4), .sel(S_4), .en(Enable_2));
  Demultiplexer #(.select(3), .disabled(0)) demultiplexer_5 (
    .out0(P_5), .out1(Q_5), .out2(R_3), .out3(S_9), .out4(T), .out5(U), .out6(V), .out7(W), .in(X_5),
    .sel(S_5), .en(Enable_3));
  Demultiplexer #(.select(3), .disabled(0)) demultiplexer_6 (
    .out0(X_7[0]), .out1(X_7[1]), .out2(X_7[2]), .out3(X_7[3]), .out4(X_7[4]), .out5(X_7[5]), .out6(X_7[6]),
    .out7(X_7[7]), .in(X_6), .sel(S_6), .en(Enable_4));

  // Notes on the sheet:
  //   Demultiplexer aus der Bibliothek
  //   DEMUX 1:2
  //   DEMUX 1:4
  //   DEMUX 1:2 mit Enable
  //   DEMUX 1:4 mit Enable
  //   DEMUX 1:8 mit Enable
  //   DEMUX 1:8 mit Enable, gebündelte Ausgänge
  //   W V U  T S R Q P
endmodule

module Mehrfach_DEMUXES__parallel (
  input  [2:0] S,
  input  Enable,
  input  [3:0] X,
  input  [3:0] X_2,
  input  [2:0] S_2,
  input  Enable_2,
  output P0,
  output Q0,
  output R0,
  output S0,
  output T0,
  output U0,
  output V0,
  output W,
  output P1,
  output Q1,
  output R1,
  output S1,
  output T1,
  output U1,
  output V1,
  output W1,
  output [3:0] P,
  output [3:0] Q,
  output [3:0] R,
  output [3:0] S_3,
  output [3:0] T,
  output P2,
  output [3:0] U,
  output Q2,
  output [3:0] V,
  output R2,
  output [3:0] W_2,
  output S2,
  output T2,
  output U2,
  output V2,
  output W2,
  output P3,
  output Q3,
  output R3,
  output S3,
  output T3,
  output U3,
  output V3,
  output W3
);

  Demultiplexer #(.select(3), .disabled(0)) demultiplexer_1 (
    .out0(P0), .out1(Q0), .out2(R0), .out3(S0), .out4(T0), .out5(U0), .out6(V0), .out7(W), .in(X[0]),
    .sel(S), .en(Enable));
  Demultiplexer #(.select(3), .disabled(0)) demultiplexer_2 (
    .out0(P1), .out1(Q1), .out2(R1), .out3(S1), .out4(T1), .out5(U1), .out6(V1), .out7(W1), .in(X[1]),
    .sel(S), .en(Enable));
  Demultiplexer #(.select(3), .disabled(0)) demultiplexer_3 (
    .out0(P2), .out1(Q2), .out2(R2), .out3(S2), .out4(T2), .out5(U2), .out6(V2), .out7(W2), .in(X[2]),
    .sel(S), .en(Enable));
  Demultiplexer #(.select(3), .disabled(0)) demultiplexer_4 (
    .out0(P3), .out1(Q3), .out2(R3), .out3(S3), .out4(T3), .out5(U3), .out6(V3), .out7(W3), .in(X[3]),
    .sel(S), .en(Enable));
  Demultiplexer #(.select(3), .width(4), .disabled(0)) demultiplexer_5 (
    .out0(P), .out1(Q), .out2(R), .out3(S_3), .out4(T), .out5(U), .out6(V), .out7(W_2), .in(X_2), .sel(S_2),
    .en(Enable_2));

  // Notes on the sheet:
  //   Mehrere parallele Demultiplexer
  //   ungebündelte Ausgänge (1-Bit Ausgänge)
  //   0
  //   =
  //   DEMUX 1:8 mit 4-Bit Ausgängen (je 4 Bit gebündelt)
endmodule

module Decoder_als_DEMUX_verwendet (
  input  X,
  input  X_2,
  input  S,
  input  Enable,
  input  S_2,
  input  Enable_2,
  input  X_3,
  input  X_4,
  input  [1:0] S_3,
  input  Enable_3,
  input  [1:0] S_4,
  input  Enable_4,
  output P,
  output P_2,
  output Q,
  output Q_2,
  output P_3,
  output P_4,
  output Q_3,
  output Q_4,
  output R,
  output R_2,
  output S_5,
  output S_6
);

  Decoder #(.select(2), .disabled(0)) decoder_1 (
    .out2(P), .out3(Q), .sel({X, S_2}), .en(Enable_2));  // open: out0, out1
  Decoder #(.select(3), .disabled(0)) decoder_2 (
    .out4(P_4), .out5(Q_4), .out6(R_2), .out7(S_6), .sel({X_3, S_4}), .en(Enable_4));  // open: out0, out1, out2, out3
  Demultiplexer #(.disabled(0)) demultiplexer_1 (.out0(P_2), .out1(Q_2), .in(X_2), .sel(S), .en(Enable));
  Demultiplexer #(.select(2), .disabled(0)) demultiplexer_2 (
    .out0(P_3), .out1(Q_3), .out2(R), .out3(S_5), .in(X_4), .sel(S_3), .en(Enable_3));

  // Notes on the sheet:
  //   Decoder als DEMUX verwendet
  //   Decoder 2:4 mit Enable
  //   Decoder 3:8 mit Enable
  //   =
  //   =
  //   DEMUX 1:2 mit Enable
  //   DEMUX 1:4 mit Enable
endmodule
