// Logisim project schaltnetze.circ as structural Verilog
module Seite_2__HA__Black_Box (
  input  x1,
  input  x0,
  output c,
  output s
);

  Seite_2__HA seite_2_ha_1 (.x1(x1), .x0(x0), .c(c), .s(s));

  // Notes on the sheet:
  //   Halbaddierer (Half Adder) in Black Box Darstellung
endmodule

module Seite_2__HA (
  input  x1,
  input  x0,
  output c,
  output s
);

  and and_1 (c, x0, x1);
  xor xor_1 (s, x1, x0);

  // Notes on the sheet:
  //   Halbaddierer
endmodule

module Seite_2__VA__Black_Box (
  input  x1,
  input  x0,
  input  cin,
  output cout,
  output s
);

  VA va_1 (.x1(x1), .x0(x0), .cin(cin), .cout(cout), .s(s));

  // Notes on the sheet:
  //   Volladdierer
endmodule

module Seite_3__VA_mit_HA (
  input  x1,
  input  x0,
  input  cin,
  output cout,
  output s
);

  wire seite_2_ha_1_c, seite_2_ha_1_s, seite_2_ha_2_c;

  Seite_2__HA seite_2_ha_1 (.x1(x1), .x0(x0), .c(seite_2_ha_1_c), .s(seite_2_ha_1_s));
  Seite_2__HA seite_2_ha_2 (.x1(seite_2_ha_1_s), .x0(cin), .c(seite_2_ha_2_c), .s(s));
  form form_1 ();

  // Notes on the sheet:
  //   Volladdierer (Full Adder) mit HA realisierbar?
  //   s'
  //   c'
  //   c
endmodule

module Seite_3__VA_mit_HA_realisiert (
  input  x1,
  input  x0,
  input  cin,
  output cout,
  output s
);

  wire seite_2_ha_1_c, seite_2_ha_1_s, seite_2_ha_2_c;

  Seite_2__HA seite_2_ha_1 (.x1(x1), .x0(x0), .c(seite_2_ha_1_c), .s(seite_2_ha_1_s));
  Seite_2__HA seite_2_ha_2 (.x1(seite_2_ha_1_s), .x0(cin), .c(seite_2_ha_2_c), .s(s));
  or or_1 (cout, seite_2_ha_1_c, seite_2_ha_2_c);

  // Notes on the sheet:
  //   Volladdierer mit HA realisiert
endmodule

module Seite_4__RCA (
  input  cin0,
  input  A0,
  input  B0,
  input  A1,
  input  B1,
  input  A2,
  input  B2,
  input  A3,
  input  B3,
  output s0,
  output s1,
  output s2,
  output s3,
  output cout3
);

  wire seite_3_va_mit_ha_realisiert_1_cout, seite_3_va_mit_ha_realisiert_2_cout,
       seite_3_va_mit_ha_realisiert_3_cout;

  Seite_3__VA_mit_HA_realisiert seite_3_va_mit_ha_realisiert_1 (
    .x1(B0), .x0(A0), .cin(cin0), .cout(seite_3_va_mit_ha_realisiert_1_cout), .s(s0));
  Seite_3__VA_mit_HA_realisiert seite_3_va_mit_ha_realisiert_2 (
    .x1(B1), .x0(A1), .cin(seite_3_va_mit_ha_realisiert_1_cout), .cout(seite_3_va_mit_ha_realisiert_2_cout),
    .s(s1));
  Seite_3__VA_mit_HA_realisiert seite_3_va_mit_ha_realisiert_3 (
    .x1(B2), .x0(A2), .cin(seite_3_va_mit_ha_realisiert_2_cout), .cout(seite_3_va_mit_ha_realisiert_3_cout),
    .s(s2));
  Seite_3__VA_mit_HA_realisiert seite_3_va_mit_ha_realisiert_4 (
    .x1(B3), .x0(A3), .cin(seite_3_va_mit_ha_realisiert_3_cout), .cout(cout3), .s(s3));

  // Notes on the sheet:
  //   Ripple Carry Adder (RCA) mit VA realisiert
  //   cout0
  //   cin1
  //   cout1
  //   cin2
  //   cout2
  //   cin3
endmodule

module Seite_6__CLAA__4_Bit (
  input  B3,
  input  A3,
  input  B2,
  input  A2,
  input  B1,
  input  A1,
  input  B0,
  input  A0,
  input  Cin0
);

  wire and_1_out, and_2_out, and_3_out, and_4_out, and_5_out, and_6_out, and_7_out, and_8_out, and_9_out,
       and_10_out, and_11_out, and_12_out, and_13_out, and_14_out, nor_1_out, nor_2_out, nor_3_out,
       nor_4_out, not_1_out, not_2_out, or_1_out, or_2_out, or_3_out, or_4_out, xnor_1_out, xnor_2_out,
       xnor_3_out, xnor_4_out, xor_1_out, xor_2_out, xor_3_out, xor_4_out;

  or or_1 (or_1_out, A3, B3);
  and and_1 (and_1_out, B3, A3);
  or or_2 (or_2_out, A2, B2);
  and and_2 (and_2_out, B2, A2);
  or or_3 (or_3_out, A1, B1);
  and and_3 (and_3_out, B1, A1);
  or or_4 (or_4_out, A0, B0);
  and and_4 (and_4_out, B0, A0);
  and and_5 (and_5_out, or_4_out, or_3_out, or_2_out, or_1_out);
  and and_6 (and_6_out, and_4_out, or_3_out, or_2_out, or_1_out);
  and and_7 (and_7_out, and_3_out, or_2_out, or_1_out);
  and and_8 (and_8_out, and_2_out, or_1_out);
  xor xor_1 (xor_1_out, or_1_out, and_1_out);
  and and_9 (and_9_out, Cin0, or_4_out, or_3_out, or_2_out);
  and and_10 (and_10_out, or_3_out, or_2_out, and_4_out);
  and and_11 (and_11_out, or_2_out, and_3_out);
  xor xor_2 (xor_2_out, or_2_out, and_2_out);
  and and_12 (and_12_out, Cin0, or_4_out, or_3_out);
  and and_13 (and_13_out, or_3_out, and_4_out);
  xor xor_3 (xor_3_out, or_3_out, and_3_out);
  and and_14 (and_14_out, Cin0, or_4_out);
  xor xor_4 (xor_4_out, or_4_out, and_4_out);
  not not_1 (not_1_out, Cin0);
  not not_2 (not_2_out, and_5_out);
  nor nor_1 (nor_1_out, and_6_out, and_7_out, and_8_out, and_1_out);
  nor nor_2 (nor_2_out, and_9_out, and_10_out, and_11_out, and_2_out);
  nor nor_3 (nor_3_out, and_12_out, and_13_out, and_3_out);
  nor nor_4 (nor_4_out, and_14_out, and_4_out);
  xnor xnor_1 (xnor_1_out, xor_1_out, nor_2_out);
  xnor xnor_2 (xnor_2_out, xor_2_out, nor_3_out);
  xnor xnor_3 (xnor_3_out, xor_3_out, nor_4_out);
  xnor xnor_4 (xnor_4_out, xor_4_out, not_1_out);
  LED nP (.in(not_2_out));
  LED nQ (.in(nor_1_out));
  LED S3 (.in(xnor_1_out));
  LED S2 (.in(xnor_2_out));
  LED S1 (.in(xnor_3_out));
  LED S0 (.in(xnor_4_out));

  // Notes on the sheet:
  //   4-Bit Carry Look Ahead Adder (CLAA)
  //   p3
  //   g3
  //   p2
  //   g2
  //   p1
  //   g1
  //   p0
  //   g0
  //   ~Cout2
  //   ~Cout1
  //   ~Cout0
endmodule

module Seite_7__16_Bit_Addierer (
  input  A15,
  input  in_2,
  input  in_3,
  input  in_4,
  input  A11,
  input  in_6,
  input  in_7,
  input  in_8,
  input  A7,
  input  in_10,
  input  in_11,
  input  in_12,
  input  A3,
  input  in_14,
  input  in_15,
  input  A0,
  input  B3,
  input  in_18,
  input  in_19,
  input  B0,
  input  B15,
  input  in_22,
  input  in_23,
  input  in_24,
  input  B11,
  input  in_26,
  input  in_27,
  input  in_28,
  input  B7,
  input  in_30,
  input  in_31,
  input  in_32,
  input  Ci
);

  wire claa_mit_cout_1_ng, claa_mit_cout_1_np, claa_mit_cout_1_s0, claa_mit_cout_1_s1, claa_mit_cout_1_s2,
       claa_mit_cout_1_s3, claa_mit_cout_2_ng, claa_mit_cout_2_np, claa_mit_cout_2_s0, claa_mit_cout_2_s1,
       claa_mit_cout_2_s2, claa_mit_cout_2_s3, claa_mit_cout_3_ng, claa_mit_cout_3_np, claa_mit_cout_3_s0,
       claa_mit_cout_3_s1, claa_mit_cout_3_s2, claa_mit_cout_3_s3, claa_mit_cout_4_cout3, claa_mit_cout_4_ng,
       claa_mit_cout_4_np, claa_mit_cout_4_s0, claa_mit_cout_4_s1, claa_mit_cout_4_s2, claa_mit_cout_4_s3,
       clag_1_cn_x, clag_1_cn_y, clag_1_cn_z;

  LED Co (.in(claa_mit_cout_4_cout3));
  LED led_1 (.in(claa_mit_cout_4_s3));
  LED led_2 (.in(claa_mit_cout_4_s2));
  LED led_3 (.in(claa_mit_cout_4_s1));
  LED led_4 (.in(claa_mit_cout_4_s0));
  LED led_5 (.in(claa_mit_cout_3_s2));
  LED led_6 (.in(claa_mit_cout_3_s3));
  LED led_7 (.in(claa_mit_cout_3_s1));
  LED led_8 (.in(claa_mit_cout_2_s1));
  LED led_9 (.in(claa_mit_cout_2_s3));
  LED led_10 (.in(claa_mit_cout_3_s0));
  LED led_11 (.in(claa_mit_cout_2_s2));
  LED led_12 (.in(claa_mit_cout_1_s2));
  LED led_13 (.in(claa_mit_cout_2_s0));
  LED led_14 (.in(claa_mit_cout_1_s3));
  CLAA_mit_Cout claa_mit_cout_1 (
    .B3(B3), .A3(A3), .B2(in_18), .A2(in_14), .B1(in_19), .A1(in_15), .B0(B0), .A0(A0), .Cin0(Ci),
    .nP(claa_mit_cout_1_np), .nG(claa_mit_cout_1_ng), .S3(claa_mit_cout_1_s3), .S2(claa_mit_cout_1_s2),
    .S1(claa_mit_cout_1_s1), .S0(claa_mit_cout_1_s0));  // open: Cout3
  LED led_15 (.in(claa_mit_cout_1_s1));
  LED led_16 (.in(claa_mit_cout_1_s0));
  CLAA_mit_Cout claa_mit_cout_2 (
    .B3(B7), .A3(A7), .B2(in_30), .A2(in_10), .B1(in_31), .A1(in_11), .B0(in_32), .A0(in_12),
    .Cin0(clag_1_cn_x), .nP(claa_mit_cout_2_np), .nG(claa_mit_cout_2_ng), .S3(claa_mit_cout_2_s3),
    .S2(claa_mit_cout_2_s2), .S1(claa_mit_cout_2_s1), .S0(claa_mit_cout_2_s0));  // open: Cout3
  CLAA_mit_Cout claa_mit_cout_3 (
    .B3(B11), .A3(A11), .B2(in_26), .A2(in_6), .B1(in_27), .A1(in_7), .B0(in_28), .A0(in_8),
    .Cin0(clag_1_cn_y), .nP(claa_mit_cout_3_np), .nG(claa_mit_cout_3_ng), .S3(claa_mit_cout_3_s3),
    .S2(claa_mit_cout_3_s2), .S1(claa_mit_cout_3_s1), .S0(claa_mit_cout_3_s0));  // open: Cout3
  CLAA_mit_Cout claa_mit_cout_4 (
    .B3(B15), .A3(A15), .B2(in_22), .A2(in_2), .B1(in_23), .A1(in_3), .B0(in_24), .A0(in_4),
    .Cin0(clag_1_cn_z), .Cout3(claa_mit_cout_4_cout3), .nP(claa_mit_cout_4_np), .nG(claa_mit_cout_4_ng),
    .S3(claa_mit_cout_4_s3), .S2(claa_mit_cout_4_s2), .S1(claa_mit_cout_4_s1), .S0(claa_mit_cout_4_s0));
  CLAG clag_1 (
    .nG0(claa_mit_cout_1_ng), .nP0(claa_mit_cout_1_np), .Ci(Ci), .nG1(claa_mit_cout_2_ng),
    .nP1(claa_mit_cout_2_np), .nG2(claa_mit_cout_3_ng), .nP2(claa_mit_cout_3_np), .nG3(claa_mit_cout_4_ng),
    .nP3(claa_mit_cout_4_np), .Cn_x(clag_1_cn_x), .Cn_y(clag_1_cn_y), .Cn_z(clag_1_cn_z));  // open: nG, nP

  // Notes on the sheet:
  //   16-Bit Addierer
endmodule

module Seite_8__Komparator__2_Bit (
  input  Y1,
  input  Y0,
  input  X1,
  input  X0,
  output X_Y,
  output X_Y_2,
  output X_Y_3
);

  wire and_1_out, and_2_out, and_3_out, and_4_out, and_5_out, and_6_out, not_1_out, not_2_out, not_3_out,
       not_4_out;

  not not_1 (not_1_out, Y0);
  not not_2 (not_2_out, Y1);
  not not_3 (not_3_out, X1);
  not not_4 (not_4_out, X0);
  and and_1 (and_1_out, Y1, not_3_out);
  and and_2 (and_2_out, Y1, Y0, not_4_out);
  and and_3 (and_3_out, Y0, not_3_out, not_4_out);
  and and_4 (and_4_out, not_2_out, X1);
  and and_5 (and_5_out, not_2_out, not_1_out, X0);
  and and_6 (and_6_out, not_1_out, X1, X0);
  or or_1 (X_Y, and_1_out, and_2_out, and_3_out);
  or or_2 (X_Y_3, and_4_out, and_5_out, and_6_out);
  nor nor_1 (X_Y_2, X_Y, X_Y_3);

  // Notes on the sheet:
  //   2-Bit Komparator
endmodule

module Seite_9__4_Bit_Magnitude_Comparator (
  input  [3:0] X,
  input  [3:0] Y,
  output X_Y,
  output X_Y_2,
  output X_Y_3
);

  _4_Bit_Magnitude_Comparator u_4_bit_magnitude_comparator_1 (
    .A3(X[3]), .B3(Y[3]), .A2(X[2]), .B2(Y[2]), .I_A_B(1'b0), .I_A_B_2(1'b1), .I_A_B_3(1'b0), .A1(X[1]),
    .B1(Y[1]), .A0(X[0]), .B0(Y[0]), .A_B(X_Y_3), .A_B_2(X_Y_2), .A_B_3(X_Y));

  // Notes on the sheet:
  //   4-Bit Magnitude Comparator
endmodule

module Seite_9__12_Bit_Magnitude_Comparator (
  input  [11:0] X,
  input  [11:0] Y,
  output X_Y,
  output X_Y_2,
  output X_Y_3
);

  wire n4_bit_magnitude_comparator_1_a_b, n4_bit_magnitude_comparator_1_a_b_2,
       n4_bit_magnitude_comparator_1_a_b_3, n4_bit_magnitude_comparator_2_a_b,
       n4_bit_magnitude_comparator_2_a_b_2, n4_bit_magnitude_comparator_2_a_b_3;

  _4_Bit_Magnitude_Comparator u_4_bit_magnitude_comparator_1 (
    .A3(X[3]), .B3(Y[3]), .A2(X[2]), .B2(Y[2]), .I_A_B(1'b0), .I_A_B_2(1'b1), .I_A_B_3(1'b0), .A1(X[1]),
    .B1(Y[1]), .A0(X[0]), .B0(Y[0]), .A_B(n4_bit_magnitude_comparator_1_a_b),
    .A_B_2(n4_bit_magnitude_comparator_1_a_b_2), .A_B_3(n4_bit_magnitude_comparator_1_a_b_3));
  _4_Bit_Magnitude_Comparator u_4_bit_magnitude_comparator_2 (
    .A3(X[7]), .B3(Y[7]), .A2(X[6]), .B2(Y[6]), .I_A_B(n4_bit_magnitude_comparator_1_a_b_3),
    .I_A_B_2(n4_bit_magnitude_comparator_1_a_b_2), .I_A_B_3(n4_bit_magnitude_comparator_1_a_b), .A1(X[5]),
    .B1(Y[5]), .A0(X[4]), .B0(Y[4]), .A_B(n4_bit_magnitude_comparator_2_a_b),
    .A_B_2(n4_bit_magnitude_comparator_2_a_b_2), .A_B_3(n4_bit_magnitude_comparator_2_a_b_3));
  _4_Bit_Magnitude_Comparator u_4_bit_magnitude_comparator_3 (
    .A3(X[11]), .B3(Y[11]), .A2(X[10]), .B2(Y[10]), .I_A_B(n4_bit_magnitude_comparator_2_a_b_3),
    .I_A_B_2(n4_bit_magnitude_comparator_2_a_b_2), .I_A_B_3(n4_bit_magnitude_comparator_2_a_b), .A1(X[9]),
    .B1(Y[9]), .A0(X[8]), .B0(Y[8]), .A_B(X_Y_3), .A_B_2(X_Y_2), .A_B_3(X_Y));

  // Notes on the sheet:
  //   12-Bit Magnitude Comparator
endmodule

module Seite_9__24_Bit_Magnitude_Comparator (
  input  [23:0] A,
  input  [23:0] B,
  output A_B,
  output A_B_2,
  output A_B_3
);

  wire n4_bit_magnitude_comparator_1_a_b, n4_bit_magnitude_comparator_1_a_b_3,
       n4_bit_magnitude_comparator_2_a_b, n4_bit_magnitude_comparator_2_a_b_3,
       n4_bit_magnitude_comparator_3_a_b, n4_bit_magnitude_comparator_3_a_b_3,
       n4_bit_magnitude_comparator_4_a_b, n4_bit_magnitude_comparator_4_a_b_3,
       n4_bit_magnitude_comparator_5_a_b, n4_bit_magnitude_comparator_5_a_b_2,
       n4_bit_magnitude_comparator_5_a_b_3;

  _4_Bit_Magnitude_Comparator u_4_bit_magnitude_comparator_1 (
    .A3(A[23]), .B3(B[23]), .A2(A[22]), .B2(B[22]), .I_A_B(B[19]), .I_A_B_2(1'b0), .I_A_B_3(A[19]),
    .A1(A[21]), .B1(B[21]), .A0(A[20]), .B0(B[20]), .A_B(n4_bit_magnitude_comparator_1_a_b),
    .A_B_3(n4_bit_magnitude_comparator_1_a_b_3));  // open: A_B_2
  _4_Bit_Magnitude_Comparator u_4_bit_magnitude_comparator_2 (
    .A3(A[18]), .B3(B[18]), .A2(A[17]), .B2(B[17]), .I_A_B(B[14]), .I_A_B_2(1'b0), .I_A_B_3(A[14]),
    .A1(A[16]), .B1(B[16]), .A0(A[15]), .B0(B[15]), .A_B(n4_bit_magnitude_comparator_2_a_b),
    .A_B_3(n4_bit_magnitude_comparator_2_a_b_3));  // open: A_B_2
  _4_Bit_Magnitude_Comparator u_4_bit_magnitude_comparator_3 (
    .A3(A[13]), .B3(B[13]), .A2(A[12]), .B2(B[12]), .I_A_B(B[9]), .I_A_B_2(1'b0), .I_A_B_3(A[9]), .A1(A[11]),
    .B1(B[11]), .A0(A[10]), .B0(B[10]), .A_B(n4_bit_magnitude_comparator_3_a_b),
    .A_B_3(n4_bit_magnitude_comparator_3_a_b_3));  // open: A_B_2
  _4_Bit_Magnitude_Comparator u_4_bit_magnitude_comparator_4 (
    .A3(A[8]), .B3(B[8]), .A2(A[7]), .B2(B[7]), .I_A_B(B[4]), .I_A_B_2(1'b0), .I_A_B_3(A[4]), .A1(A[6]),
    .B1(B[6]), .A0(A[5]), .B0(B[5]), .A_B(n4_bit_magnitude_comparator_4_a_b),
    .A_B_3(n4_bit_magnitude_comparator_4_a_b_3));  // open: A_B_2
  _4_Bit_Magnitude_Comparator u_4_bit_magnitude_comparator_5 (
    .A3(A[3]), .B3(B[3]), .A2(A[2]), .B2(B[2]), .I_A_B(1'b0), .I_A_B_2(1'b1), .I_A_B_3(1'b0), .A1(A[1]),
    .B1(B[1]), .A0(A[0]), .B0(B[0]), .A_B(n4_bit_magnitude_comparator_5_a_b),
    .A_B_2(n4_bit_magnitude_comparator_5_a_b_2), .A_B_3(n4_bit_magnitude_comparator_5_a_b_3));
  _4_Bit_Magnitude_Comparator u_4_bit_magnitude_comparator_6 (
    .A3(n4_bit_magnitude_comparator_1_a_b), .B3(n4_bit_magnitude_comparator_1_a_b_3),
    .A2(n4_bit_magnitude_comparator_2_a_b), .B2(n4_bit_magnitude_comparator_2_a_b_3),
    .I_A_B(n4_bit_magnitude_comparator_5_a_b_3), .I_A_B_2(n4_bit_magnitude_comparator_5_a_b_2),
    .I_A_B_3(n4_bit_magnitude_comparator_5_a_b), .A1(n4_bit_magnitude_comparator_3_a_b),
    .B1(n4_bit_magnitude_comparator_3_a_b_3), .A0(n4_bit_magnitude_comparator_4_a_b),
    .B0(n4_bit_magnitude_comparator_4_a_b_3), .A_B(A_B_3), .A_B_2(A_B_2), .A_B_3(A_B));

  // Notes on the sheet:
  //   24-Bit Magnitude Comparator
endmodule

module Seite_9__MUX_visualisiert (
  input  I0,
  input  I1,
  input  I2,
  input  I3,
  input  S1,
  input  S0,
  output Y
);

  wire display1_1_out_12, display1_1_out_13, display1_1_out_14, display1_1_out_16, display1_1_out_17,
       display1_1_out_18, display1_1_out_19, display1_1_out_20, display1_1_out_21, display1_1_out_22,
       display1_1_out_23, display1_1_out_25, display1_1_out_26, display1_1_out_27, display1_1_out_28,
       display1_1_out_29, display1_1_out_30, display1_1_out_31, display1_1_out_32, display1_1_out_33,
       display1_1_red_led0, display1_1_red_led1, display1_1_red_led2, display1_1_red_led3, display1_1_y;

  display1 display1_1 (
    .I0(I0), .I1(I1), .I2(I2), .I3(I3), .RED_LED0(display1_1_red_led0), .RED_LED1(display1_1_red_led1),
    .RED_LED2(display1_1_red_led2), .RED_LED3(display1_1_red_led3), .out_12(display1_1_out_12),
    .out_13(display1_1_out_13), .out_14(display1_1_out_14), .Y(display1_1_y), .out_16(display1_1_out_16),
    .out_17(display1_1_out_17), .out_18(display1_1_out_18), .out_19(display1_1_out_19),
    .out_20(display1_1_out_20), .out_21(display1_1_out_21), .out_22(display1_1_out_22),
    .out_23(display1_1_out_23), .out_25(display1_1_out_25), .out_26(display1_1_out_26),
    .out_27(display1_1_out_27), .out_28(display1_1_out_28), .out_29(display1_1_out_29),
    .out_30(display1_1_out_30), .out_31(display1_1_out_31), .out_32(display1_1_out_32),
    .out_33(display1_1_out_33), .out_24(Y), .S1(S1), .S0(S0), .nEnable(1'b0));
  LED I0_selected (.in(display1_1_red_led0));
  LED I1_selected (.in(display1_1_red_led1));
  LED I2_selected (.in(display1_1_red_led2));
  LED I3_selected (.in(display1_1_red_led3));
  LED led_1 (.in(display1_1_out_12));
  LED led_2 (.in(display1_1_out_17));
  LED led_3 (.in(display1_1_out_18));
  LED led_4 (.in(display1_1_out_19));
  LED led_5 (.in(display1_1_out_26));
  LED led_6 (.in(display1_1_out_28));
  LED led_7 (.in(display1_1_out_29));
  LED led_8 (.in(display1_1_out_33));
  LED led_9 (.in(display1_1_out_13));
  LED led_10 (.in(display1_1_out_14));
  LED led_11 (.in(display1_1_out_20));
  LED led_12 (.in(display1_1_out_16));
  LED led_13 (.in(display1_1_out_21));
  LED led_14 (.in(display1_1_out_22));
  LED led_15 (.in(display1_1_out_23));
  LED led_16 (.in(display1_1_out_25));
  LED led_17 (.in(display1_1_out_27));
  LED led_18 (.in(display1_1_out_30));
  LED led_19 (.in(display1_1_out_31));
  LED led_20 (.in(display1_1_out_32));
  LED led_21 (.in(display1_1_y));
  table1 table1_1 ();

  // Notes on the sheet:
  //   MUX: Visualisierung des Datenflusses nach Y
endmodule

module Seite_10__4_to_1_MUX__Black_Box (
  input  S1,
  input  S0,
  input  I0,
  input  I1,
  input  I2,
  input  I3,
  input  nEnable
);

  wire n4_to_1_mux_1_y;

  _4_to_1_MUX u_4_to_1_mux_1 (
    .S1(S1), .S0(S0), .I0(I0), .I1(I1), .I2(I2), .I3(I3), .nEnable(nEnable), .Y(n4_to_1_mux_1_y));
  LED Y (.in(n4_to_1_mux_1_y));

  // Notes on the sheet:
  //   4-zu-1 Multiplexer
endmodule

module Seite_10__MUX_mit__Enable_visualisiert (
  input  I0,
  input  I1,
  input  I2,
  input  I3,
  input  nEnable,
  input  S1,
  input  S0,
  output Y
);

  wire display1_1_out_12, display1_1_out_13, display1_1_out_14, display1_1_out_16, display1_1_out_17,
       display1_1_out_18, display1_1_out_19, display1_1_out_20, display1_1_out_21, display1_1_out_22,
       display1_1_out_23, display1_1_out_25, display1_1_out_26, display1_1_out_27, display1_1_out_28,
       display1_1_out_29, display1_1_out_30, display1_1_out_31, display1_1_out_32, display1_1_out_33,
       display1_1_red_led0, display1_1_red_led1, display1_1_red_led2, display1_1_red_led3, display1_1_y;

  LED I0_selected (.in(display1_1_red_led0));
  display1 display1_1 (
    .I0(I0), .I1(I1), .I2(I2), .I3(I3), .RED_LED0(display1_1_red_led0), .RED_LED1(display1_1_red_led1),
    .RED_LED2(display1_1_red_led2), .RED_LED3(display1_1_red_led3), .out_12(display1_1_out_12),
    .out_13(display1_1_out_13), .out_14(display1_1_out_14), .Y(display1_1_y), .out_16(display1_1_out_16),
    .out_17(display1_1_out_17), .out_18(display1_1_out_18), .out_19(display1_1_out_19),
    .out_20(display1_1_out_20), .out_21(display1_1_out_21), .out_22(display1_1_out_22),
    .out_23(display1_1_out_23), .out_25(display1_1_out_25), .out_26(display1_1_out_26),
    .out_27(display1_1_out_27), .out_28(display1_1_out_28), .out_29(display1_1_out_29),
    .out_30(display1_1_out_30), .out_31(display1_1_out_31), .out_32(display1_1_out_32),
    .out_33(display1_1_out_33), .out_24(Y), .S1(S1), .S0(S0), .nEnable(nEnable));
  LED I1_selected (.in(display1_1_red_led1));
  LED I2_selected (.in(display1_1_red_led2));
  LED I3_selected (.in(display1_1_red_led3));
  LED led_1 (.in(display1_1_out_12));
  LED led_2 (.in(display1_1_out_17));
  LED led_3 (.in(display1_1_out_18));
  LED led_4 (.in(display1_1_out_19));
  LED led_5 (.in(display1_1_out_26));
  LED led_6 (.in(display1_1_out_28));
  LED led_7 (.in(display1_1_out_29));
  LED led_8 (.in(display1_1_out_33));
  LED led_9 (.in(display1_1_out_13));
  LED led_10 (.in(display1_1_out_14));
  LED led_11 (.in(display1_1_out_20));
  LED led_12 (.in(display1_1_out_16));
  LED led_13 (.in(display1_1_out_21));
  LED led_14 (.in(display1_1_out_22));
  LED led_15 (.in(display1_1_out_23));
  LED led_16 (.in(display1_1_out_25));
  LED led_17 (.in(display1_1_out_27));
  LED led_18 (.in(display1_1_out_30));
  LED led_19 (.in(display1_1_out_31));
  LED led_20 (.in(display1_1_out_32));
  LED led_21 (.in(display1_1_y));
  table2 table2_1 ();

  // Notes on the sheet:
  //   MUX mit ~Enable: Visualisierung des Datenflusses nach Y
endmodule

module Seite_11__3_to_8_Decoder__Black_Box (
  input  X0,
  input  X1,
  input  X2,
  input  nEnable,
  input  X0_2,
  input  X1_2,
  input  X2_2,
  input  Disable
);

  wire n3_to_8_decoder_1_ny0, n3_to_8_decoder_1_ny1, n3_to_8_decoder_1_ny2, n3_to_8_decoder_1_ny3,
       n3_to_8_decoder_1_ny4, n3_to_8_decoder_1_ny5, n3_to_8_decoder_1_ny6, n3_to_8_decoder_1_ny7,
       n3_to_8_decoder_2_ny0, n3_to_8_decoder_2_ny1, n3_to_8_decoder_2_ny2, n3_to_8_decoder_2_ny3,
       n3_to_8_decoder_2_ny4, n3_to_8_decoder_2_ny5, n3_to_8_decoder_2_ny6, n3_to_8_decoder_2_ny7, not_1_out,
       not_2_out, not_3_out, not_4_out, not_5_out, not_6_out, not_7_out, not_8_out;

  _3_to_8_Decoder u_3_to_8_decoder_1 (
    .A(X0), .B(X1), .C(X2), .nEnable(nEnable), .nY0(n3_to_8_decoder_1_ny0), .nY1(n3_to_8_decoder_1_ny1),
    .nY2(n3_to_8_decoder_1_ny2), .nY3(n3_to_8_decoder_1_ny3), .nY4(n3_to_8_decoder_1_ny4),
    .nY5(n3_to_8_decoder_1_ny5), .nY6(n3_to_8_decoder_1_ny6), .nY7(n3_to_8_decoder_1_ny7));
  _3_to_8_Decoder u_3_to_8_decoder_2 (
    .A(X0_2), .B(X1_2), .C(X2_2), .nEnable(Disable), .nY0(n3_to_8_decoder_2_ny0),
    .nY1(n3_to_8_decoder_2_ny1), .nY2(n3_to_8_decoder_2_ny2), .nY3(n3_to_8_decoder_2_ny3),
    .nY4(n3_to_8_decoder_2_ny4), .nY5(n3_to_8_decoder_2_ny5), .nY6(n3_to_8_decoder_2_ny6),
    .nY7(n3_to_8_decoder_2_ny7));
  LED nY0 (.in(n3_to_8_decoder_1_ny0));
  LED nY1 (.in(n3_to_8_decoder_1_ny1));
  LED nY2 (.in(n3_to_8_decoder_1_ny2));
  LED nY3 (.in(n3_to_8_decoder_1_ny3));
  LED nY4 (.in(n3_to_8_decoder_1_ny4));
  LED nY5 (.in(n3_to_8_decoder_1_ny5));
  LED nY6 (.in(n3_to_8_decoder_1_ny6));
  LED nY7 (.in(n3_to_8_decoder_1_ny7));
  not not_1 (not_1_out, n3_to_8_decoder_2_ny0);
  LED Y0 (.in(not_1_out));
  LED Y1 (.in(not_2_out));
  not not_2 (not_2_out, n3_to_8_decoder_2_ny1);
  LED Y2 (.in(not_3_out));
  not not_3 (not_3_out, n3_to_8_decoder_2_ny2);
  not not_4 (not_4_out, n3_to_8_decoder_2_ny3);
  LED Y3 (.in(not_4_out));
  LED Y4 (.in(not_5_out));
  not not_5 (not_5_out, n3_to_8_decoder_2_ny4);
  LED Y5 (.in(not_6_out));
  not not_6 (not_6_out, n3_to_8_decoder_2_ny5);
  not not_7 (not_7_out, n3_to_8_decoder_2_ny6);
  LED Y6 (.in(not_7_out));
  LED Y7 (.in(not_8_out));
  not not_8 (not_8_out, n3_to_8_decoder_2_ny7);

  // Notes on the sheet:
  //   3-zu-8 Dekoder
endmodule

module \Seite_11__Multiplexte_1_Bit_Kanäle  (
  input  S1,
  input  S0,
  input  I0,
  input  I1,
  input  I2,
  input  I3
);

  wire n3_to_8_decoder_1_ny0, n3_to_8_decoder_1_ny1, n3_to_8_decoder_1_ny2, n3_to_8_decoder_1_ny3,
       n3_to_8_decoder_1_ny4, n3_to_8_decoder_1_ny5, n3_to_8_decoder_1_ny6, n3_to_8_decoder_1_ny7,
       n4_to_1_mux_1_y;

  _4_to_1_MUX u_4_to_1_mux_1 (
    .S1(S1), .S0(S0), .I0(I0), .I1(I1), .I2(I2), .I3(I3), .nEnable(1'b0), .Y(n4_to_1_mux_1_y));
  _3_to_8_Decoder u_3_to_8_decoder_1 (
    .A(S0), .B(S1), .C(n4_to_1_mux_1_y), .nEnable(1'b0), .nY0(n3_to_8_decoder_1_ny0),
    .nY1(n3_to_8_decoder_1_ny1), .nY2(n3_to_8_decoder_1_ny2), .nY3(n3_to_8_decoder_1_ny3),
    .nY4(n3_to_8_decoder_1_ny4), .nY5(n3_to_8_decoder_1_ny5), .nY6(n3_to_8_decoder_1_ny6),
    .nY7(n3_to_8_decoder_1_ny7));
  LED u_I0 (.in(n3_to_8_decoder_1_ny0));
  LED u_I1 (.in(n3_to_8_decoder_1_ny1));
  LED u_I2 (.in(n3_to_8_decoder_1_ny2));
  LED u_I3 (.in(n3_to_8_decoder_1_ny3));
  LED nI0 (.in(n3_to_8_decoder_1_ny4));
  LED nI1 (.in(n3_to_8_decoder_1_ny5));
  LED nI2 (.in(n3_to_8_decoder_1_ny6));
  LED nI3 (.in(n3_to_8_decoder_1_ny7));

  // Notes on the sheet:
  //   Kanalmultiplexing
  //   Selector Lines
endmodule

module Demo_Kanalmultiplexing (
  output I0,
  output I1,
  output I2,
  output I3
);

  wire and_1_out, and_2_out, and_3_out, and_4_out, clock_1_out, display1_1_out_12, display1_1_out_13,
       display1_1_out_14, display1_1_out_16, display1_1_out_17, display1_1_out_18, display1_1_out_19,
       display1_1_out_20, display1_1_out_21, display1_1_out_22, display1_1_out_23, display1_1_out_24,
       display1_1_out_25, display1_1_out_26, display1_1_out_27, display1_1_out_28, display1_1_out_29,
       display1_1_out_30, display1_1_out_31, display1_1_out_32, display1_1_out_33, display1_1_red_led0,
       display1_1_red_led1, display1_1_red_led2, display1_1_red_led3, display1_1_y, display2_1_out_10,
       display2_1_out_11, display2_1_out_12, display2_1_out_14, display2_1_out_15, display2_1_out_16,
       display2_1_out_17, display2_1_out_18, display2_1_out_19, display2_1_out_20, display2_1_out_21,
       display2_1_out_22, display2_1_out_23, display2_1_out_25, display2_1_out_26, display2_1_out_27,
       display2_1_out_28, display2_1_out_29, display2_1_out_30, display2_1_out_32, display2_1_out_33,
       display2_1_red_led0, display2_1_red_led1, display2_1_red_led2, display2_1_red_led3, rom_1_data,
       rom_2_data, rom_3_data, rom_4_data;
  wire [1:0] counter_5_q;
  wire [4:0] counter_1_q, counter_2_q, counter_3_q, counter_4_q;

  Counter #(.width(5), .max('h1f)) counter_1 (.Q(counter_1_q), .clk(and_1_out));  // open: load, D, count, carry, clr
  Counter #(.width(5), .max('h1f)) counter_2 (.Q(counter_2_q), .clk(and_2_out));  // open: load, D, count, carry, clr
  Counter #(.width(5), .max('h1f)) counter_3 (.Q(counter_3_q), .clk(and_3_out));  // open: load, D, count, carry, clr
  Counter #(.width(5), .max('h1f)) counter_4 (.Q(counter_4_q), .clk(and_4_out));  // open: load, D, count, carry, clr
  Counter #(.width(2), .max('h3)) counter_5 (.Q(counter_5_q), .clk(clock_1_out));  // open: load, D, count, carry, clr
  Clock clock_1 (.out(clock_1_out));
  and and_1 (and_1_out, ~counter_5_q[0], ~counter_5_q[1]);  // AND_Gate
  and and_2 (and_2_out, counter_5_q[0], ~counter_5_q[1]);  // AND_Gate
  and and_3 (and_3_out, ~counter_5_q[0], counter_5_q[1]);  // AND_Gate
  and and_4 (and_4_out, counter_5_q[0], counter_5_q[1]);
  display1 display1_1 (
    .I0(rom_1_data), .I1(rom_2_data), .I2(rom_3_data), .I3(rom_4_data), .RED_LED0(display1_1_red_led0),
    .RED_LED1(display1_1_red_led1), .RED_LED2(display1_1_red_led2), .RED_LED3(display1_1_red_led3),
    .out_12(display1_1_out_12), .out_13(display1_1_out_13), .out_14(display1_1_out_14), .Y(display1_1_y),
    .out_16(display1_1_out_16), .out_17(display1_1_out_17), .out_18(display1_1_out_18),
    .out_19(display1_1_out_19), .out_20(display1_1_out_20), .out_21(display1_1_out_21),
    .out_22(display1_1_out_22), .out_23(display1_1_out_23), .out_25(display1_1_out_25),
    .out_26(display1_1_out_26), .out_27(display1_1_out_27), .out_28(display1_1_out_28),
    .out_29(display1_1_out_29), .out_30(display1_1_out_30), .out_31(display1_1_out_31),
    .out_32(display1_1_out_32), .out_33(display1_1_out_33), .out_24(display1_1_out_24), .S1(counter_5_q[1]),
    .S0(counter_5_q[0]), .nEnable(1'b0));
  LED I0_selected (.in(display1_1_red_led0));
  ROM #(.addrWidth(5), .dataWidth(1)) rom_1 (.addr(counter_1_q), .data(rom_1_data));  // open: sel
  LED I1_selected (.in(display1_1_red_led1));
  ROM #(.addrWidth(5), .dataWidth(1)) rom_2 (.addr(counter_2_q), .data(rom_2_data));  // open: sel
  ROM #(.addrWidth(5), .dataWidth(1)) rom_3 (.addr(counter_3_q), .data(rom_3_data));  // open: sel
  LED I2_selected (.in(display1_1_red_led2));
  ROM #(.addrWidth(5), .dataWidth(1)) rom_4 (.addr(counter_4_q), .data(rom_4_data));  // open: sel
  LED I3_selected (.in(display1_1_red_led3));
  LED led_1 (.in(display1_1_out_12));
  LED led_2 (.in(display1_1_out_13));
  LED led_3 (.in(display1_1_out_17));
  LED led_4 (.in(display1_1_out_18));
  LED led_5 (.in(display1_1_out_19));
  LED led_6 (.in(display1_1_out_26));
  LED led_7 (.in(display1_1_out_28));
  LED led_8 (.in(display1_1_out_29));
  LED led_9 (.in(display1_1_out_32));
  LED led_10 (.in(display1_1_out_33));
  LED led_11 (.in(display1_1_out_14));
  LED led_12 (.in(display1_1_out_20));
  LED led_13 (.in(display1_1_out_16));
  LED led_14 (.in(display1_1_out_21));
  LED led_15 (.in(display1_1_out_22));
  LED led_16 (.in(display1_1_y));
  LED led_17 (.in(display1_1_out_23));
  LED led_18 (.in(display1_1_out_25));
  LED led_19 (.in(display1_1_out_27));
  LED led_20 (.in(display1_1_out_30));
  LED led_21 (.in(display1_1_out_31));
  arrow arrow_1 ();
  display2 display2_1 (
    .RED_LED0(display2_1_red_led0), .RED_LED1(display2_1_red_led1), .RED_LED2(display2_1_red_led2),
    .RED_LED3(display2_1_red_led3), .out_10(display2_1_out_10), .out_11(display2_1_out_11),
    .out_12(display2_1_out_12), .out_14(display2_1_out_14), .out_15(display2_1_out_15),
    .out_16(display2_1_out_16), .out_17(display2_1_out_17), .out_18(display2_1_out_18),
    .out_19(display2_1_out_19), .out_20(display2_1_out_20), .out_21(display2_1_out_21),
    .out_22(display2_1_out_22), .out_23(display2_1_out_23), .out_25(display2_1_out_25),
    .out_26(display2_1_out_26), .out_27(display2_1_out_27), .out_28(display2_1_out_28),
    .out_29(display2_1_out_29), .out_30(display2_1_out_30), .out_32(display2_1_out_32),
    .out_33(display2_1_out_33), .S1(counter_5_q[1]), .S0(counter_5_q[0]), .Y(display1_1_out_24),
    .nEnable(1'b0), .I0(I0), .I1(I1), .I2(I2), .I3(I3));
  LED led_22 (.in(display2_1_out_17));
  LED led_23 (.in(display2_1_out_20));
  LED led_24 (.in(display2_1_out_21));
  LED led_25 (.in(display2_1_out_22));
  LED led_26 (.in(display2_1_out_25));
  LED led_27 (.in(display2_1_out_10));
  LED led_28 (.in(display2_1_out_11));
  LED led_29 (.in(display2_1_out_12));
  LED led_30 (.in(display2_1_out_14));
  LED led_31 (.in(display2_1_out_18));
  LED led_32 (.in(display2_1_out_19));
  LED led_33 (.in(display2_1_out_23));
  LED led_34 (.in(display2_1_out_26));
  LED led_35 (.in(display2_1_out_29));
  LED led_36 (.in(display2_1_out_30));
  LED led_37 (.in(display2_1_out_32));
  LED led_38 (.in(display2_1_out_33));
  LED I0_selected_2 (.in(display2_1_red_led0));
  LED I1_selected_2 (.in(display2_1_red_led1));
  LED led_39 (.in(display2_1_out_15));
  LED led_40 (.in(display2_1_out_16));
  LED led_41 (.in(display2_1_out_27));
  LED led_42 (.in(display2_1_out_28));
  LED I2_selected_2 (.in(display2_1_red_led2));
  LED I3_selected_2 (.in(display2_1_red_led3));

  // Notes on the sheet:
  //   Demo Kanalmultiplexing
  //   contents of rom_1 (hex, n*v repeats v):
  //   1 0 1 0 1 1 1 0 1 0 1 0 1 0 1 0 1 1 0 5*1 0 1 4*0 1
  //   contents of rom_2 (hex, n*v repeats v):
  //   0 0 1 1 1 0 0 4*1 0 1 1 0 1 1 0 0 1 1 1 0 0 1 1 0 1 0 1 0 1
  //   contents of rom_3 (hex, n*v repeats v):
  //   10*0 1 1 1 0 0 1 1 1 0 1
  //   contents of rom_4 (hex, n*v repeats v):
  //   4*1 4*0 1 1 1 0 1 1 0 1 5*0 4*1 0 0 0 1 1 0 1
endmodule

module Seite_12__4_Bit_ALU (
  input  S0,
  input  S1,
  input  S2,
  input  S3,
  input  B3,
  input  A3,
  input  B2,
  input  A2,
  input  B1,
  input  A1,
  input  B0,
  input  A0,
  input  M,
  input  Cn,
  output nG,
  output Cn_4,
  output nP,
  output nF3,
  output nF2,
  output A_B,
  output nF1,
  output nF0
);

  wire and_1_out, and_2_out, and_3_out, and_4_out, and_5_out, and_6_out, and_7_out, and_8_out, and_9_out,
       and_10_out, and_11_out, and_12_out, and_13_out, and_14_out, and_15_out, and_16_out, and_17_out,
       and_18_out, and_19_out, and_20_out, and_22_out, and_23_out, and_24_out, and_25_out, and_26_out,
       and_27_out, and_28_out, and_29_out, and_30_out, and_31_out, and_32_out, and_33_out, and_34_out,
       nand_1_out, nor_1_out, nor_2_out, nor_3_out, nor_4_out, nor_5_out, nor_6_out, nor_7_out, nor_8_out,
       nor_10_out, nor_11_out, nor_12_out, not_1_out, not_2_out, not_3_out, not_4_out, not_5_out, not_6_out,
       not_7_out, not_8_out, not_9_out;

  not not_1 (not_1_out, B3);
  not not_2 (not_2_out, B2);
  not not_3 (not_3_out, B1);
  not not_4 (not_4_out, B0);
  not not_5 (not_5_out, M);
  and and_1 (and_1_out, B3, S3, A3);
  and and_2 (and_2_out, A3, S2, not_1_out);
  and and_3 (and_3_out, not_1_out, S1);
  and and_4 (and_4_out, S0, B3);
  and and_5 (and_5_out, B2, S3, A2);
  and and_6 (and_6_out, A2, S2, not_2_out);
  and and_7 (and_7_out, not_2_out, S1);
  and and_8 (and_8_out, S0, B2);
  and and_9 (and_9_out, B1, S3, A1);
  and and_10 (and_10_out, A1, S2, not_3_out);
  and and_11 (and_11_out, not_3_out, S1);
  and and_12 (and_12_out, S0, B1);
  and and_13 (and_13_out, B0, S3, A0);
  and and_14 (and_14_out, A0, S2, not_4_out);
  and and_15 (and_15_out, not_4_out, S1);
  and and_16 (and_16_out, S0, B0);
  nor nor_1 (nor_1_out, and_1_out, and_2_out);
  nor nor_2 (nor_2_out, and_3_out, and_4_out, A3);
  nor nor_3 (nor_3_out, and_5_out, and_6_out);
  nor nor_4 (nor_4_out, and_7_out, and_8_out, A2);
  nor nor_5 (nor_5_out, and_9_out, and_10_out);
  nor nor_6 (nor_6_out, and_11_out, and_12_out, A1);
  nor nor_7 (nor_7_out, and_13_out, and_14_out);
  nor nor_8 (nor_8_out, and_15_out, and_16_out, A0);
  not not_6 (not_6_out, nor_2_out);
  not not_7 (not_7_out, nor_4_out);
  not not_8 (not_8_out, nor_6_out);
  not not_9 (not_9_out, nor_8_out);
  and and_17 (and_17_out, nor_1_out, nor_4_out);
  and and_18 (and_18_out, nor_1_out, nor_3_out, nor_6_out);
  and and_19 (and_19_out, nor_1_out, nor_4_out, nor_5_out, nor_8_out);
  and and_20 (and_20_out, nor_1_out, nor_3_out, nor_5_out, nor_7_out, Cn);
  and and_21 (nP, nor_1_out, nor_3_out, nor_5_out, nor_7_out);
  and and_22 (and_22_out, nor_3_out, nor_5_out, nor_7_out, Cn, not_5_out);
  and and_23 (and_23_out, nor_3_out, nor_5_out, nor_8_out, not_5_out);
  and and_24 (and_24_out, nor_3_out, nor_6_out, not_5_out);
  and and_25 (and_25_out, nor_4_out, not_5_out);
  and and_26 (and_26_out, nor_5_out, nor_7_out, Cn, not_5_out);
  and and_27 (and_27_out, nor_5_out, nor_8_out, not_5_out);
  and and_28 (and_28_out, nor_6_out, not_5_out);
  and and_29 (and_29_out, Cn, nor_7_out, not_5_out);
  and and_30 (and_30_out, nor_8_out, not_5_out);
  nand nand_1 (nand_1_out, not_5_out, Cn);
  nor nor_9 (nG, nor_2_out, and_17_out, and_18_out, and_19_out);
  and and_31 (and_31_out, nor_1_out, not_6_out);
  nor nor_10 (nor_10_out, and_22_out, and_23_out, and_24_out, and_25_out);
  and and_32 (and_32_out, nor_3_out, not_7_out);
  nor nor_11 (nor_11_out, and_26_out, and_27_out, and_28_out);
  and and_33 (and_33_out, nor_5_out, not_8_out);
  nor nor_12 (nor_12_out, and_29_out, and_30_out);
  and and_34 (and_34_out, nor_7_out, not_9_out);
  nand nand_2 (Cn_4, nG, and_20_out);
  xor xor_1 (nF3, and_31_out, nor_10_out);
  xor xor_2 (nF2, and_32_out, nor_11_out);
  xor xor_3 (nF1, and_33_out, nor_12_out);
  xor xor_4 (nF0, and_34_out, nand_1_out);
  and and_35 (A_B, nF2, nF3, nF0, nF1);

  // Notes on the sheet:
  //   4-Bit ALU
endmodule

module Seite_12__4_Bit_ALU__Black_Box (
  input  S3,
  input  S2,
  input  S1,
  input  S0,
  input  A3,
  input  A2,
  input  A1,
  input  A0,
  input  B3,
  input  B2,
  input  B1,
  input  B0,
  input  M,
  input  Cn
);

  wire seite_12_4_bit_alu_1_cn_4, seite_12_4_bit_alu_1_nf0, seite_12_4_bit_alu_1_nf1,
       seite_12_4_bit_alu_1_nf2, seite_12_4_bit_alu_1_nf3, seite_12_4_bit_alu_1_ng, seite_12_4_bit_alu_1_np;

  Seite_12__4_Bit_ALU seite_12_4_bit_alu_1 (
    .S0(S0), .S1(S1), .S2(S2), .S3(S3), .B3(B3), .A3(A3), .B2(B2), .A2(A2), .B1(B1), .A1(A1), .B0(B0),
    .A0(A0), .M(M), .Cn(Cn), .nG(seite_12_4_bit_alu_1_ng), .Cn_4(seite_12_4_bit_alu_1_cn_4),
    .nP(seite_12_4_bit_alu_1_np), .nF3(seite_12_4_bit_alu_1_nf3), .nF2(seite_12_4_bit_alu_1_nf2),
    .nF1(seite_12_4_bit_alu_1_nf1), .nF0(seite_12_4_bit_alu_1_nf0));  // open: A_B
  LED nG (.in(seite_12_4_bit_alu_1_ng));
  LED nP (.in(seite_12_4_bit_alu_1_np));
  LED Cn_4 (.in(seite_12_4_bit_alu_1_cn_4));
  LED R3 (.in(seite_12_4_bit_alu_1_nf3));
  LED R2 (.in(seite_12_4_bit_alu_1_nf2));
  LED R1 (.in(seite_12_4_bit_alu_1_nf1));
  LED R0 (.in(seite_12_4_bit_alu_1_nf0));

  // Notes on the sheet:
  //   4-Bit ALU
endmodule

module VA (
  input  x1,
  input  x0,
  input  cin,
  output cout,
  output s
);

  wire seite_2_ha_1_c, seite_2_ha_1_s, seite_2_ha_2_c;

  Seite_2__HA seite_2_ha_1 (.x1(x1), .x0(x0), .c(seite_2_ha_1_c), .s(seite_2_ha_1_s));
  Seite_2__HA seite_2_ha_2 (.x1(seite_2_ha_1_s), .x0(cin), .c(seite_2_ha_2_c), .s(s));
  or or_1 (cout, seite_2_ha_1_c, seite_2_ha_2_c);

  // Notes on the sheet:
  //   Volladdierer mit HA realisiert
endmodule

module CLAG (
  input  nG0,
  input  nP0,
  input  Ci,
  input  nG1,
  input  nP1,
  input  nG2,
  input  nP2,
  input  nG3,
  input  nP3,
  output Cn_x,
  output Cn_y,
  output Cn_z,
  output nG,
  output nP
);

  wire and_1_out, and_2_out, and_3_out, and_4_out, and_5_out, and_6_out, and_7_out, and_8_out, and_9_out,
       and_10_out, and_11_out, and_12_out, and_13_out, not_1_out;

  not not_1 (not_1_out, Ci);
  and and_1 (and_1_out, nG0, nP0);
  and and_2 (and_2_out, nG0, not_1_out);
  and and_3 (and_3_out, nG1, nP1);
  and and_4 (and_4_out, nG0, nP0, nG1);
  and and_5 (and_5_out, not_1_out, nG0, nG1);
  and and_6 (and_6_out, nG2, nP2);
  and and_7 (and_7_out, nG1, nP1, nG2);
  and and_8 (and_8_out, nG0, nP0, nG1, nG2);
  and and_9 (and_9_out, not_1_out, nG0, nG1, nG2);
  and and_10 (and_10_out, nG3, nP3);
  and and_11 (and_11_out, nG2, nP2, nG3);
  and and_12 (and_12_out, nG1, nP1, nG2, nG3);
  and and_13 (and_13_out, nG0, nG1, nG2, nG3);
  nor nor_1 (Cn_x, and_1_out, and_2_out);
  nor nor_2 (Cn_y, and_3_out, and_4_out, and_5_out);
  nor nor_3 (Cn_z, and_6_out, and_7_out, and_8_out, and_9_out);
  or or_1 (nG, and_10_out, and_11_out, and_12_out, and_13_out);
  or or_2 (nP, nP0, nP1, nP2, nP3);

  // Notes on the sheet:
  //   Carry Look Ahead Generator
endmodule

module CLAA_mit_Cout (
  input  B3,
  input  A3,
  input  B2,
  input  A2,
  input  B1,
  input  A1,
  input  B0,
  input  A0,
  input  Cin0,
  output Cout3,
  output nP,
  output nG,
  output S3,
  output S2,
  output S1,
  output S0
);

  wire and_1_out, and_2_out, and_3_out, and_4_out, and_5_out, and_6_out, and_7_out, and_8_out, and_9_out,
       and_10_out, and_11_out, and_12_out, and_13_out, and_14_out, and_15_out, nor_1_out, nor_2_out,
       nor_3_out, not_1_out, or_1_out, or_2_out, or_3_out, or_4_out, or_5_out, xor_1_out, xor_2_out,
       xor_3_out, xor_4_out;

  or or_1 (or_1_out, A3, B3);
  and and_1 (and_1_out, B3, A3);
  or or_2 (or_2_out, A2, B2);
  and and_2 (and_2_out, B2, A2);
  or or_3 (or_3_out, A1, B1);
  and and_3 (and_3_out, B1, A1);
  or or_4 (or_4_out, A0, B0);
  and and_4 (and_4_out, B0, A0);
  and and_5 (and_5_out, or_4_out, or_3_out, or_2_out, or_1_out);
  and and_6 (and_6_out, and_4_out, or_3_out, or_2_out, or_1_out);
  and and_7 (and_7_out, and_3_out, or_2_out, or_1_out);
  and and_8 (and_8_out, and_2_out, or_1_out);
  and and_9 (and_9_out, Cin0, or_4_out, or_3_out, or_2_out);
  and and_10 (and_10_out, or_3_out, or_2_out, and_4_out);
  and and_11 (and_11_out, or_2_out, and_3_out);
  and and_12 (and_12_out, Cin0, or_4_out, or_3_out);
  and and_13 (and_13_out, or_3_out, and_4_out);
  and and_14 (and_14_out, Cin0, or_4_out);
  not not_1 (not_1_out, Cin0);
  xor xor_1 (xor_1_out, or_1_out, and_1_out);
  xor xor_2 (xor_2_out, or_2_out, and_2_out);
  xor xor_3 (xor_3_out, or_3_out, and_3_out);
  xor xor_4 (xor_4_out, or_4_out, and_4_out);
  and and_15 (and_15_out, Cin0, and_5_out);
  not not_2 (nP, and_5_out);
  or or_5 (or_5_out, and_6_out, and_7_out, and_8_out, and_1_out);
  nor nor_1 (nor_1_out, and_9_out, and_10_out, and_11_out, and_2_out);
  nor nor_2 (nor_2_out, and_12_out, and_13_out, and_3_out);
  nor nor_3 (nor_3_out, and_14_out, and_4_out);
  or or_6 (Cout3, and_15_out, or_5_out);
  not not_3 (nG, or_5_out);
  xnor xnor_1 (S3, xor_1_out, nor_1_out);
  xnor xnor_2 (S2, xor_2_out, nor_2_out);
  xnor xnor_3 (S1, xor_3_out, nor_3_out);
  xnor xnor_4 (S0, xor_4_out, not_1_out);

  // Notes on the sheet:
  //   Carry Look Ahead Adder (CLAA) mit Cout
  //   p3
  //   g3
  //   p2
  //   g2
  //   p1
  //   g1
  //   p0
  //   g0
  //   ~Cout2
  //   ~Cout1
  //   ~Cout0
endmodule

module _4_Bit_Magnitude_Comparator (
  input  A3,
  input  B3,
  input  A2,
  input  B2,
  input  I_A_B,
  input  I_A_B_2,
  input  I_A_B_3,
  input  A1,
  input  B1,
  input  A0,
  input  B0,
  output A_B,
  output A_B_2,
  output A_B_3
);

  wire and_1_out, and_2_out, and_3_out, and_4_out, and_5_out, and_6_out, and_7_out, and_8_out, and_9_out,
       and_10_out, and_11_out, and_12_out, and_13_out, and_14_out, and_15_out, and_16_out, and_17_out,
       and_18_out, and_19_out, and_20_out, nand_1_out, nand_2_out, nand_3_out, nand_4_out, nor_1_out,
       nor_2_out, nor_3_out, nor_4_out;

  nand nand_1 (nand_1_out, A3, B3);
  nand nand_2 (nand_2_out, A2, B2);
  nand nand_3 (nand_3_out, A1, B1);
  nand nand_4 (nand_4_out, A0, B0);
  and and_1 (and_1_out, A3, nand_1_out);
  and and_2 (and_2_out, nand_1_out, B3);
  and and_3 (and_3_out, A2, nand_2_out);
  and and_4 (and_4_out, nand_2_out, B2);
  and and_5 (and_5_out, A1, nand_3_out);
  and and_6 (and_6_out, nand_3_out, B1);
  and and_7 (and_7_out, A0, nand_4_out);
  and and_8 (and_8_out, nand_4_out, B0);
  nor nor_1 (nor_1_out, and_1_out, and_2_out);
  nor nor_2 (nor_2_out, and_3_out, and_4_out);
  nor nor_3 (nor_3_out, and_5_out, and_6_out);
  nor nor_4 (nor_4_out, and_7_out, and_8_out);
  and and_9 (and_9_out, B3, nand_1_out);
  and and_10 (and_10_out, B2, nand_2_out, nor_1_out);
  and and_11 (and_11_out, B1, nand_3_out, nor_1_out, nor_2_out);
  and and_12 (and_12_out, B0, nand_4_out, nor_1_out, nor_2_out, nor_3_out);
  and and_13 (and_13_out, nor_1_out, nor_2_out, nor_3_out, nor_4_out, I_A_B);
  and and_14 (and_14_out, nor_1_out, nor_2_out, nor_3_out, nor_4_out, I_A_B_2);
  and and_15 (and_15_out, I_A_B_2, nor_4_out, nor_3_out, nor_2_out, nor_1_out);
  and and_16 (and_16_out, I_A_B_3, nor_4_out, nor_2_out, nor_3_out, nor_1_out);
  and and_17 (and_17_out, nor_3_out, nor_2_out, nor_1_out, nand_4_out, A0);
  and and_18 (and_18_out, nor_2_out, nor_1_out, nand_3_out, A1);
  and and_19 (and_19_out, nor_1_out, nand_2_out, A2);
  and and_20 (and_20_out, nand_1_out, A3);
  and and_21 (A_B, ~and_9_out, ~and_10_out, ~and_11_out, ~and_12_out, ~and_13_out, ~and_14_out);  // AND_Gate
  and and_22 (A_B_2, nor_1_out, nor_2_out, I_A_B_2, nor_3_out, nor_4_out);
  and and_23 (A_B_3, ~and_15_out, ~and_16_out, ~and_17_out, ~and_18_out, ~and_19_out, ~and_20_out);  // AND_Gate

  // Notes on the sheet:
  //   4-Bit Magnitude Comparator
endmodule

module _4_to_1_MUX (
  input  S1,
  input  S0,
  input  I0,
  input  I1,
  input  I2,
  input  I3,
  input  nEnable,
  output Y
);

  wire and_1_out, and_2_out, and_3_out, and_4_out, not_1_out, not_2_out, not_3_out;

  not not_1 (not_1_out, S1);
  not not_2 (not_2_out, S0);
  not not_3 (not_3_out, nEnable);
  and and_1 (and_1_out, I0, not_1_out, not_2_out, not_3_out);
  and and_2 (and_2_out, I1, not_1_out, S0, not_3_out);
  and and_3 (and_3_out, I2, S1, not_2_out, not_3_out);
  and and_4 (and_4_out, I3, S1, S0, not_3_out);
  or or_1 (Y, and_1_out, and_2_out, and_3_out, and_4_out);

  // Notes on the sheet:
  //   4-zu-1 Multiplexer
endmodule

module _3_to_8_Decoder (
  input  A,
  input  B,
  input  C,
  input  nEnable,
  output nY0,
  output nY1,
  output nY2,
  output nY3,
  output nY4,
  output nY5,
  output nY6,
  output nY7
);

  wire not_1_out, not_2_out, not_3_out, or_1_out, or_2_out, or_3_out, or_4_out, or_5_out, or_6_out, or_7_out,
       or_8_out;

  not not_1 (not_1_out, A);
  not not_2 (not_2_out, B);
  not not_3 (not_3_out, C);
  or or_1 (or_1_out, A, B, C);
  or or_2 (or_2_out, not_1_out, B, C);
  or or_3 (or_3_out, A, not_2_out, C);
  or or_4 (or_4_out, not_1_out, not_2_out, C);
  or or_5 (or_5_out, A, B, not_3_out);
  or or_6 (or_6_out, not_1_out, B, not_3_out);
  or or_7 (or_7_out, A, not_2_out, not_3_out);
  or or_8 (or_8_out, not_1_out, not_2_out, not_3_out);
  or or_9 (nY0, or_1_out, nEnable);
  or or_10 (nY1, or_2_out, nEnable);
  or or_11 (nY2, or_3_out, nEnable);
  or or_12 (nY3, or_4_out, nEnable);
  or or_13 (nY4, or_5_out, nEnable);
  or or_14 (nY5, or_6_out, nEnable);
  or or_15 (nY6, or_7_out, nEnable);
  or or_16 (nY7, or_8_out, nEnable);

  // Notes on the sheet:
  //   3-zu-8 Dekoder
endmodule

module display1 (
  input  I0,
  input  I1,
  input  I2,
  input  S1,
  input  S0,
  input  nEnable,
  input  I3,
  output RED_LED0,
  output RED_LED1,
  output RED_LED2,
  output RED_LED3,
  output out_12,
  output out_13,
  output out_14,
  output Y,
  output out_16,
  output out_17,
  output out_18,
  output out_19,
  output out_20,
  output out_21,
  output out_22,
  output out_23,
  output out_24,
  output out_25,
  output out_26,
  output out_27,
  output out_28,
  output out_29,
  output out_30,
  output out_31,
  output out_32,
  output out_33
);

  wire not_1_out;

  _4_to_1_MUX u_4_to_1_mux_1 (.S1(S1), .S0(S0), .I0(I0), .I1(I1), .I2(I2), .I3(I3), .nEnable(nEnable), .Y(Y));
  not not_1 (not_1_out, nEnable);
  Decoder #(.select(2), .disabled(0), .enable("false")) decoder_1 (
    .out0(RED_LED0), .out1(RED_LED1), .out2(RED_LED2), .out3(RED_LED3), .sel({S1, S0}));
  and and_1 (out_12, RED_LED0, not_1_out, I0);
  and and_2 (out_17, RED_LED1, not_1_out, I1);
  and and_3 (out_23, RED_LED2, not_1_out, I2);
  and and_4 (out_27, RED_LED3, not_1_out, I3);
  or or_1 (out_24, out_12, out_17, out_23, out_27);

  assign out_13 = out_12;
  assign out_14 = out_12;
  assign out_16 = out_12;
  assign out_18 = out_17;
  assign out_19 = out_17;
  assign out_20 = out_12;
  assign out_21 = out_17;
  assign out_22 = out_17;
  assign out_25 = out_23;
  assign out_26 = out_23;
  assign out_28 = out_23;
  assign out_29 = out_23;
  assign out_30 = out_27;
  assign out_31 = out_27;
  assign out_32 = out_27;
  assign out_33 = out_27;
endmodule

module display2 (
  input  S1,
  input  S0,
  input  Y,
  input  nEnable,
  output RED_LED0,
  output RED_LED1,
  output RED_LED2,
  output RED_LED3,
  output I0,
  output out_10,
  output out_11,
  output out_12,
  output I1,
  output out_14,
  output out_15,
  output out_16,
  output out_17,
  output out_18,
  output out_19,
  output out_20,
  output out_21,
  output out_22,
  output out_23,
  output I2,
  output out_25,
  output out_26,
  output out_27,
  output out_28,
  output out_29,
  output out_30,
  output I3,
  output out_32,
  output out_33
);

  wire n3_to_8_decoder_1_ny0, n3_to_8_decoder_1_ny1, n3_to_8_decoder_1_ny2, n3_to_8_decoder_1_ny3, not_1_out;

  _3_to_8_Decoder u_3_to_8_decoder_1 (
    .A(S0), .B(S1), .C(Y), .nEnable(nEnable), .nY0(n3_to_8_decoder_1_ny0), .nY1(n3_to_8_decoder_1_ny1),
    .nY2(n3_to_8_decoder_1_ny2), .nY3(n3_to_8_decoder_1_ny3));  // open: nY4, nY5, nY6, nY7
  not not_1 (not_1_out, nEnable);
  Decoder #(.select(2), .disabled(0), .enable("false")) decoder_1 (
    .out0(RED_LED0), .out1(RED_LED1), .out2(RED_LED2), .out3(RED_LED3), .sel({S1, S0}));
  and and_1 (I0, RED_LED0, not_1_out, n3_to_8_decoder_1_ny0);
  and and_2 (I1, RED_LED1, not_1_out, n3_to_8_decoder_1_ny1);
  and and_3 (I2, RED_LED2, not_1_out, n3_to_8_decoder_1_ny2);
  and and_4 (I3, RED_LED3, not_1_out, n3_to_8_decoder_1_ny3);
  or or_1 (out_21, I3, I2, I1, I0);

  assign out_10 = I0;
  assign out_11 = I0;
  assign out_12 = I0;
  assign out_14 = I0;
  assign out_15 = I1;
  assign out_16 = I1;
  assign out_17 = I0;
  assign out_18 = I1;
  assign out_19 = I1;
  assign out_20 = I1;
  assign out_22 = I2;
  assign out_23 = I2;
  assign out_25 = I3;
  assign out_26 = I2;
  assign out_27 = I2;
  assign out_28 = I2;
  assign out_29 = I3;
  assign out_30 = I3;
  assign out_32 = I3;
  assign out_33 = I3;
endmodule

module DEMUX_visualisiert (
  input  Y,
  input  S1,
  input  S0,
  output I0,
  output I1,
  output I2,
  output I3
);

  wire display2_1_out_10, display2_1_out_11, display2_1_out_12, display2_1_out_14, display2_1_out_15,
       display2_1_out_16, display2_1_out_17, display2_1_out_18, display2_1_out_19, display2_1_out_20,
       display2_1_out_21, display2_1_out_22, display2_1_out_23, display2_1_out_25, display2_1_out_26,
       display2_1_out_27, display2_1_out_28, display2_1_out_29, display2_1_out_30, display2_1_out_32,
       display2_1_out_33, display2_1_red_led0, display2_1_red_led1, display2_1_red_led2, display2_1_red_led3;

  display2 display2_1 (
    .RED_LED0(display2_1_red_led0), .RED_LED1(display2_1_red_led1), .RED_LED2(display2_1_red_led2),
    .RED_LED3(display2_1_red_led3), .out_10(display2_1_out_10), .out_11(display2_1_out_11),
    .out_12(display2_1_out_12), .out_14(display2_1_out_14), .out_15(display2_1_out_15),
    .out_16(display2_1_out_16), .out_17(display2_1_out_17), .out_18(display2_1_out_18),
    .out_19(display2_1_out_19), .out_20(display2_1_out_20), .out_21(display2_1_out_21),
    .out_22(display2_1_out_22), .out_23(display2_1_out_23), .out_25(display2_1_out_25),
    .out_26(display2_1_out_26), .out_27(display2_1_out_27), .out_28(display2_1_out_28),
    .out_29(display2_1_out_29), .out_30(display2_1_out_30), .out_32(display2_1_out_32),
    .out_33(display2_1_out_33), .S1(S1), .S0(S0), .Y(Y), .nEnable(1'b0), .I0(I0), .I1(I1), .I2(I2), .I3(I3));
  LED led_1 (.in(display2_1_out_21));
  LED led_2 (.in(display2_1_out_11));
  LED led_3 (.in(display2_1_out_12));
  LED led_4 (.in(display2_1_out_14));
  LED led_5 (.in(display2_1_out_17));
  LED led_6 (.in(display2_1_out_19));
  LED led_7 (.in(display2_1_out_20));
  LED led_8 (.in(display2_1_out_22));
  LED led_9 (.in(display2_1_out_23));
  LED led_10 (.in(display2_1_out_25));
  LED led_11 (.in(display2_1_out_29));
  LED led_12 (.in(display2_1_out_30));
  LED led_13 (.in(display2_1_out_32));
  LED led_14 (.in(display2_1_out_10));
  LED led_15 (.in(display2_1_out_15));
  LED led_16 (.in(display2_1_out_16));
  LED led_17 (.in(display2_1_out_18));
  LED led_18 (.in(display2_1_out_26));
  LED led_19 (.in(display2_1_out_27));
  LED led_20 (.in(display2_1_out_28));
  LED led_21 (.in(display2_1_out_33));
  LED I0_selected (.in(display2_1_red_led0));
  LED I1_selected (.in(display2_1_red_led1));
  LED I2_selected (.in(display2_1_red_led2));
  LED I3_selected (.in(display2_1_red_led3));

  // Notes on the sheet:
  //   DEMUX: Visualisierung des Datenflusses von Y
endmodule

module \Visualisierung_multiplexte_1_Bit_Kanäle  (
  input  I0,
  input  I1,
  input  I2,
  input  I3,
  input  S1,
  input  S0,
  output I0_2,
  output I1_2,
  output I2_2,
  output I3_2
);

  wire display1_1_out_12, display1_1_out_13, display1_1_out_14, display1_1_out_16, display1_1_out_17,
       display1_1_out_18, display1_1_out_19, display1_1_out_20, display1_1_out_21, display1_1_out_22,
       display1_1_out_23, display1_1_out_24, display1_1_out_25, display1_1_out_26, display1_1_out_27,
       display1_1_out_28, display1_1_out_29, display1_1_out_30, display1_1_out_31, display1_1_out_32,
       display1_1_out_33, display1_1_red_led0, display1_1_red_led1, display1_1_red_led2, display1_1_red_led3,
       display1_1_y, display2_1_out_10, display2_1_out_11, display2_1_out_12, display2_1_out_14,
       display2_1_out_15, display2_1_out_16, display2_1_out_17, display2_1_out_18, display2_1_out_19,
       display2_1_out_20, display2_1_out_21, display2_1_out_22, display2_1_out_23, display2_1_out_25,
       display2_1_out_26, display2_1_out_27, display2_1_out_28, display2_1_out_29, display2_1_out_30,
       display2_1_out_32, display2_1_out_33, display2_1_red_led0, display2_1_red_led1, display2_1_red_led2,
       display2_1_red_led3;

  LED I0_selected (.in(display1_1_red_led0));
  display1 display1_1 (
    .I0(I0), .I1(I1), .I2(I2), .I3(I3), .RED_LED0(display1_1_red_led0), .RED_LED1(display1_1_red_led1),
    .RED_LED2(display1_1_red_led2), .RED_LED3(display1_1_red_led3), .out_12(display1_1_out_12),
    .out_13(display1_1_out_13), .out_14(display1_1_out_14), .Y(display1_1_y), .out_16(display1_1_out_16),
    .out_17(display1_1_out_17), .out_18(display1_1_out_18), .out_19(display1_1_out_19),
    .out_20(display1_1_out_20), .out_21(display1_1_out_21), .out_22(display1_1_out_22),
    .out_23(display1_1_out_23), .out_25(display1_1_out_25), .out_26(display1_1_out_26),
    .out_27(display1_1_out_27), .out_28(display1_1_out_28), .out_29(display1_1_out_29),
    .out_30(display1_1_out_30), .out_31(display1_1_out_31), .out_32(display1_1_out_32),
    .out_33(display1_1_out_33), .out_24(display1_1_out_24), .S1(S1), .S0(S0), .nEnable(1'b0));
  LED I1_selected (.in(display1_1_red_led1));
  LED I2_selected (.in(display1_1_red_led2));
  LED I3_selected (.in(display1_1_red_led3));
  LED led_1 (.in(display1_1_out_12));
  LED led_2 (.in(display1_1_out_17));
  LED led_3 (.in(display1_1_out_18));
  LED led_4 (.in(display1_1_out_19));
  LED led_5 (.in(display1_1_out_26));
  LED led_6 (.in(display1_1_out_28));
  LED led_7 (.in(display1_1_out_29));
  LED led_8 (.in(display1_1_out_33));
  LED led_9 (.in(display1_1_out_13));
  LED led_10 (.in(display1_1_out_14));
  LED led_11 (.in(display1_1_out_20));
  LED led_12 (.in(display1_1_out_16));
  LED led_13 (.in(display1_1_out_21));
  LED led_14 (.in(display1_1_out_22));
  LED led_15 (.in(display1_1_out_23));
  LED led_16 (.in(display1_1_out_25));
  LED led_17 (.in(display1_1_out_27));
  LED led_18 (.in(display1_1_out_30));
  LED led_19 (.in(display1_1_out_31));
  LED led_20 (.in(display1_1_out_32));
  LED led_21 (.in(display1_1_y));
  display2 display2_1 (
    .RED_LED0(display2_1_red_led0), .RED_LED1(display2_1_red_led1), .RED_LED2(display2_1_red_led2),
    .RED_LED3(display2_1_red_led3), .out_10(display2_1_out_10), .out_11(display2_1_out_11),
    .out_12(display2_1_out_12), .out_14(display2_1_out_14), .out_15(display2_1_out_15),
    .out_16(display2_1_out_16), .out_17(display2_1_out_17), .out_18(display2_1_out_18),
    .out_19(display2_1_out_19), .out_20(display2_1_out_20), .out_21(display2_1_out_21),
    .out_22(display2_1_out_22), .out_23(display2_1_out_23), .out_25(display2_1_out_25),
    .out_26(display2_1_out_26), .out_27(display2_1_out_27), .out_28(display2_1_out_28),
    .out_29(display2_1_out_29), .out_30(display2_1_out_30), .out_32(display2_1_out_32),
    .out_33(display2_1_out_33), .S1(S1), .S0(S0), .Y(display1_1_out_24), .nEnable(1'b0), .I0(I0_2),
    .I1(I1_2), .I2(I2_2), .I3(I3_2));
  LED led_22 (.in(display2_1_out_14));
  LED led_23 (.in(display2_1_out_17));
  LED led_24 (.in(display2_1_out_20));
  LED led_25 (.in(display2_1_out_21));
  LED led_26 (.in(display2_1_out_22));
  LED led_27 (.in(display2_1_out_25));
  LED led_28 (.in(display2_1_out_29));
  LED led_29 (.in(display2_1_out_10));
  LED led_30 (.in(display2_1_out_11));
  LED led_31 (.in(display2_1_out_12));
  LED led_32 (.in(display2_1_out_16));
  LED led_33 (.in(display2_1_out_18));
  LED led_34 (.in(display2_1_out_19));
  LED led_35 (.in(display2_1_out_23));
  LED led_36 (.in(display2_1_out_26));
  LED led_37 (.in(display2_1_out_27));
  LED led_38 (.in(display2_1_out_30));
  LED led_39 (.in(display2_1_out_32));
  LED led_40 (.in(display2_1_out_33));
  LED I0_selected_2 (.in(display2_1_red_led0));
  LED I1_selected_2 (.in(display2_1_red_led1));
  LED led_41 (.in(display2_1_out_15));
  LED led_42 (.in(display2_1_out_28));
  LED I2_selected_2 (.in(display2_1_red_led2));
  LED I3_selected_2 (.in(display2_1_red_led3));

  // Notes on the sheet:
  //   Kanalmultiplexing
endmodule

module asdf (
  input  in_1,
  input  in_2,
  output out_3
);

  wire and_1_out;

  and and_1 (and_1_out, in_1, in_2);
  not not_1 (out_3, and_1_out);
endmodule

module myBlackboxAufruf (
  input  in_1,
  input  in_2,
  output out_3
);

  asdf asdf_1 (.in_1(in_1), .in_2(in_2), .out_3(out_3));
endmodule
