// Logisim project counterTemplates.circ as structural Verilog: 6 circuits, main circuit 4 bit mod counter
module _4_bit_mod_counter (
  input  S,
  input  R,
  input  En,
  input  CP,
  output Q3,
  output Q2,
  output Q1,
  output Q0,
  output nQ3,
  output nQ2,
  output nQ1,
  output nQ0
);

  wire undriven, undriven_2, undriven_3, undriven_4, undriven_5, undriven_6, undriven_7, undriven_8,
       undriven_9, undriven_10, undriven_11, undriven_12;

  LED D3 (.in(undriven));
  LED D1 (.in(undriven_2));
  LED D2 (.in(undriven_12));
  LED D0 (.in(undriven_3));
  onPosEdge onposedge_1 ();
  rising_edge_D_FF rising_edge_d_ff_1 (
    .Q(Q3), .C(CP), .D(undriven), .S(undriven_4), .R(undriven_8), .Enable(1'b1), .nQ(nQ3));
  rising_edge_D_FF rising_edge_d_ff_2 (
    .Q(Q2), .C(CP), .D(undriven_12), .S(undriven_5), .R(undriven_9), .Enable(1'b1), .nQ(nQ2));
  rising_edge_D_FF rising_edge_d_ff_3 (
    .Q(Q1), .C(CP), .D(undriven_2), .S(undriven_6), .R(undriven_10), .Enable(1'b1), .nQ(nQ1));
  rising_edge_D_FF rising_edge_d_ff_4 (
    .Q(Q0), .C(CP), .D(undriven_3), .S(undriven_7), .R(undriven_11), .Enable(1'b1), .nQ(nQ0));
endmodule

module _3_bit_mod_counter (
  input  S,
  input  R,
  input  En,
  input  CP,
  output Q2,
  output Q1,
  output Q0,
  output nQ2,
  output nQ1,
  output nQ0
);

  wire undriven, undriven_2, undriven_3, undriven_4, undriven_5, undriven_6, undriven_7, undriven_8,
       undriven_9;

  LED D2 (.in(undriven));
  LED D1 (.in(undriven_2));
  LED D0 (.in(undriven_3));
  onPosEdge onposedge_1 ();
  rising_edge_D_FF rising_edge_d_ff_1 (
    .Q(Q2), .C(CP), .D(undriven), .S(undriven_4), .R(undriven_7), .Enable(1'b1), .nQ(nQ2));
  rising_edge_D_FF rising_edge_d_ff_2 (
    .Q(Q1), .C(CP), .D(undriven_2), .S(undriven_5), .R(undriven_8), .Enable(1'b1), .nQ(nQ1));
  rising_edge_D_FF rising_edge_d_ff_3 (
    .Q(Q0), .C(CP), .D(undriven_3), .S(undriven_6), .R(undriven_9), .Enable(1'b1), .nQ(nQ0));
endmodule

module rising_edge_D_FF (
  input  C,
  input  D,
  input  S,
  input  Enable,
  input  R,
  output Q,
  output nQ
);

  D_Flip_Flop d_ff_1 (.clk(C), .D(D), .Q(Q), .Qn(nQ), .preset(S), .en(Enable), .reset(R));
endmodule

module rising_edge_D_FF_mirrored (
  input  C,
  input  D,
  input  S,
  input  Enable,
  input  R,
  output Q,
  output nQ
);

  D_Flip_Flop d_ff_1 (.clk(C), .D(D), .Q(Q), .Qn(nQ), .preset(S), .en(Enable), .reset(R));
endmodule

module onPosEdge (
);


  // Notes on the sheet:
  //   Positive edge symbol
endmodule

module arrow (
);


  // Notes on the sheet:
  //   Arrow
endmodule
