// Logisim project entwicklungRSFF.circ as structural Verilog
module main (
  input  S,
  input  S_2,
  input  Q1_t,
  input  Q1_t_2,
  input  Q2_t,
  input  Q2_t_2,
  input  R,
  input  R_2,
  output Q2_t_1,
  output Q2_t_1_2,
  output Q1_t_1,
  output Q1_t_1_2,
  output Q2_t_1_3,
  output Q1_t_1_3
);

  wire and_1_out, button_1_out, comparator_1_eq, comparator_1_gt, comparator_1_lt, comparator_2_eq,
       comparator_2_gt, comparator_2_lt, or_1_out, or_2_out;
  wire [3:0] counter_1_q;

  Counter #(.width(4), .max('hf)) counter_1 (.Q(counter_1_q), .clk(button_1_out));  // open: load, D, count, carry, clr
  Button button_1 (.out(button_1_out));
  // Probe on counter_1_q
  // Probe on counter_1_q[3]
  // Probe on counter_1_q[2]
  nor nor_1 (Q2_t_1, S, Q1_t);
  nor nor_2 (Q1_t_1, Q2_t, R);
  // Probe on counter_1_q[1]
  // Probe on counter_1_q[0]
  nor nor_3 (Q2_t_1_3, counter_1_q[3], counter_1_q[0]);
  Red_Box red_box_1 ();
  Blue_Box blue_box_1 ();
  nor nor_4 (Q1_t_1_3, counter_1_q[1], counter_1_q[2]);
  Truth_Table truth_table_1 ();
  Little_Red_Box little_red_box_1 ();
  Little_Red_Box little_red_box_2 ();
  Little_Red_Box little_red_box_3 ();
  Little_Red_Box little_red_box_4 ();
  Little_Red_Box little_red_box_5 ();
  Comparator #(.width(1)) comparator_1 (
    .a(Q2_t_1_3), .b(counter_1_q[1]), .gt(comparator_1_gt), .eq(comparator_1_eq), .lt(comparator_1_lt));
  Comparator #(.width(1)) comparator_2 (
    .a(counter_1_q[0]), .b(Q1_t_1_3), .gt(comparator_2_gt), .eq(comparator_2_eq), .lt(comparator_2_lt));
  LED gleich (.in(comparator_1_eq));
  LED gleich_2 (.in(comparator_2_eq));
  Little_Red_Box little_red_box_6 ();
  Little_Red_Box little_red_box_7 ();
  Little_Red_Box little_red_box_8 ();
  Little_Red_Box little_red_box_9 ();
  Little_Red_Box little_red_box_10 ();
  LED ungleich (.in(or_1_out));
  or or_1 (or_1_out, comparator_1_gt, comparator_1_lt);
  or or_2 (or_2_out, comparator_2_lt, comparator_2_gt);
  LED nicht_stabil (.in(or_2_out));
  LED \paarweise_gleich___stabil__grün  (.in(and_1_out));
  and and_1 (and_1_out, comparator_1_eq, comparator_2_eq);
  nor nor_5 (Q2_t_1_2, S_2, Q1_t_2);
  Red_Box red_box_2 ();
  Blue_Box blue_box_2 ();
  nor nor_6 (Q1_t_1_2, Q2_t_2, R_2);
endmodule
