// Logisim project schaltwerke - flipflops.circ as structural Verilog
module RS_FF__Eigenbau (
  input  x0___S,
  input  x1___R,
  output Q,
  output nQ
);

  wire nor_1_out, nor_2_out;

  SN_Box sn_box_1 ();
  Delay_Box delay_box_1 (.in_1(nor_1_out), .out_2(nQ));
  Delay_Box delay_box_2 (.in_1(nor_2_out), .out_2(Q));
  nor nor_1 (nor_1_out, x0___S, Q);
  nor nor_2 (nor_2_out, nQ, x1___R);

  // Notes on the sheet:
  //   RS-FF in Schaltwerk-Darstellung gemäss Skript
  //   z1_t
  //   Bemerkung:
  //   Logisim tut sich schwer mit Initialisierungen bei Rückkopplungen,
  //   daher bei Error-Meldungen vorerst S zweimal betätigen (on - off).
  //   Werden hier S=1 und R=1 gesetzt, so sind beide Ausgänge gleichzeitig
  //   0 oder 1, ein Widerspruch zu den Bezeichnungen Q und ~Q. Daher wird
  //   R=S=1 verboten.
  //   z0_t
  //   Schaltnetz
  //   Delay
  //   Delay
  //   z0_t+1
  //   z1_t+1
endmodule

module RS_FF_als_Black_Box (
  input  S,
  input  R,
  output Q,
  output nQ
);

  RS_FF__Eigenbau rs_ff_eigenbau_1 (.x0___S(S), .x1___R(R), .nQ(nQ), .Q(Q));

  // Notes on the sheet:
  //   RS-FF in Black-Box-Darstellung
  //   Bemerkung:
  //   Logisim tut sich schwer mit Initialisierungen bei Rückkopplungen,
  //   daher bei Error-Meldungen vorerst S zweimal betätigen (on - off).
  //   Werden hier S=1 und R=1 gesetzt, so sind beide Ausgänge gleichzeitig
  //   0 oder 1, ein Widerspruch zu den Bezeichnungen Q und ~Q. Daher wird
  //   R=S=1 verboten.
endmodule

module RS_FF_als_BB_aus_Bibliothek (
  input  S,
  input  R,
  output Q,
  output nQ
);

  RS_FF__aus_Bibliothek rs_ff_aus_bibliothek_1 (.S(S), .R(R), .Q(Q), .nQ(nQ));

  // Notes on the sheet:
  //   RS-FF in Black-Box-Darstellung mit Bibliotheks-RS-FF
  //   Bemerkung:
  //   Das RS-FF aus der Bibliothek hat keine Schwierigkeiten mit Anfangsbedingungen:
  //   Logisim initialisiert das FF mit Q=0.
  //   Zudem findet Logisim für die Situation R=S=1 eine Vorranglösung, womit zumindest
  //   die Ausgangsbezeichnungen Q und ~Q nicht mehr widersprüchlich sind.
endmodule

module \RS_FF_mit_R__und_S_Eingängen_verbunden  (
  input  S,
  output Q,
  output nQ
);

  wire not_1_out;

  RS_FF__aus_Bibliothek rs_ff_aus_bibliothek_1 (.S(S), .R(not_1_out), .Q(Q), .nQ(nQ));
  not not_1 (not_1_out, S);

  // Notes on the sheet:
  //   RS-FF mit R- und S-Eingang verbunden
  //   Bemerkung:
  //   Diese Schaltung entspricht einem zustandsgesteuerten D-FF.
  //   Logisim initialisiert das FF mit Q=0.
endmodule

module D_FF__zustandsgesteuert (
  input  D,
  input  C,
  output Q,
  output nQ
);

  Zustandsgesteuertes_D_FF_reduziert__aus_Bibl zustandsgesteuertes_d_ff_reduziert_aus_bibl_1 (
    .C(C), .D(D), .Q(Q), .nQ(nQ));

  // Notes on the sheet:
  //   D-FF in Black-Box-Darstellung
  //   Bemerkung:
  //   D-FF zustandsgesteuert.
  //   Für C=1 arbeitet das D-FF im Transparent-Mode: Q folgt D.
  //   Für C=0 wird/ist Q unveränderbar.
endmodule

module D_FF_erweitert__zustandsgesteuert (
  input  D,
  input  C,
  input  nEnable,
  output Q,
  output nQ
);

  wire not_1_out, Reset_out, Set_out;

  Zustandsgesteuertes_D_FF__aus_Bibl zustandsgesteuertes_d_ff_aus_bibl_1 (
    .C(C), .D(D), .S(Set_out), .Enable(not_1_out), .R(Reset_out), .Q(Q), .nQ(nQ));
  not not_1 (not_1_out, nEnable);
  Button Set (.out(Set_out));
  Button Reset (.out(Reset_out));

  // Notes on the sheet:
  //   D-FF mit weiteren Eingängen in Black-Box-Darstellung
  //   Bemerkung:
  //   D-FF zustandsgesteuert.
  //   Für C=1 arbeitet das D-FF im Transparent-Mode: Q folgt D.
  //   Für C=0 wird/ist Q unveränderbar.
  //   ~Enable wurde tief aktiv gewählt, weil Logisim beim Aufstarten alle Eingänge tief setzt:
  //   Damit ist das D-FF sofort enabled.
  //   S und R wirken mit höchster Priorität, auch dann, wenn das D-FF nicht enabled ist.
  //   Die Tasten verhindern, dass S und R gleichzeitig bedient werden können.
endmodule

module D_FF__Pos__1_Flanken_getriggert (
  input  D,
  input  C,
  output Q,
  output nQ
);

  \Positiv_1_flankengetriggertes_D_FF_ohne_Hilfseingänge  \positiv_1_flankengetriggertes_d_ff_ohne_hilfseingänge_1  (
    .C(C), .D(D), .Q(Q), .nQ(nQ));

  // Notes on the sheet:
  //   D-FF, positiv 1-Flanken-getriggert
  //   Bemerkung:
  //   Auf steigende Flanke (= positive Flanke) wird der Wert von D detektiert, gespeichert und
  //   sofort an Q angezeigt.
  //   Für C=0 oder C=1 oder auf die fallende Flanke (= negative Flanke) von C bleibt Q unverändert.
endmodule

module D_FF_erweitert__Pos__1_Flanken_getriggert (
  input  D,
  input  C,
  input  nEnable,
  output Q,
  output nQ
);

  wire not_1_out, Reset_out, Set_out;

  Positiv_1_flankengetriggertes_D_FF positiv_1_flankengetriggertes_d_ff_1 (
    .Q(Q), .C(C), .D(D), .S(Set_out), .R(Reset_out), .Enable(not_1_out), .nQ(nQ));
  not not_1 (not_1_out, nEnable);
  Button Set (.out(Set_out));
  Button Reset (.out(Reset_out));

  // Notes on the sheet:
  //   D-FF, positiv 1-Flanken-getriggert
  //   Bemerkung:
  //   Auf steigende Flanke (= positive Flanke) wird der Wert von D detektiert, gespeichert und
  //   sofort an Q angezeigt.
  //   Für C=0 oder C=1 oder auf die fallende Flanke (= negative Flanke) von C bleibt Q unverändert.
  //   ~Enable wurde tief aktiv gewählt, weil Logisim beim Aufstarten alle Eingänge tief setzt:
  //   Damit ist das D-FF sofort enabled.
  //   S und R wirken mit höchster Priorität, auch dann wenn das D-FF nicht enabled ist.
  //   Die Wahl der Tasten hier verhindern, dass S und R gleichzeitig bedient werden können.
endmodule

module D_FF__Neg__1_Flanken_getriggert (
  input  D,
  input  C,
  input  nEnable,
  output Q,
  output nQ
);

  wire not_1_out, Reset_out, Set_out;

  Negativ_1_flankengetriggertes_D_FF negativ_1_flankengetriggertes_d_ff_1 (
    .C(C), .D(D), .S(Set_out), .Enable(not_1_out), .R(Reset_out), .Q(Q), .nQ(nQ));
  not not_1 (not_1_out, nEnable);
  Button Set (.out(Set_out));
  Button Reset (.out(Reset_out));

  // Notes on the sheet:
  //   D-FF, negativ 1-Flanken-getriggert
  //   Bemerkung:
  //   Auf fallende Flanke (= negative Flanke) wird der Wert von D detektiert, gespeichert und
  //   sofort an Q angezeigt.
  //   Für C=0 oder C=1 oder auf die steigende Flanke (= positive Flanke) von C bleibt Q unverändert.
  //   ~Enable wurde tief aktiv gewählt, weil Logisim beim Aufstarten alle Eingänge tief setzt:
  //   Damit ist das D-FF sofort enabled.
  //   S und R wirken mit höchster Priorität, auch dann wenn das D-FF nicht enabled ist.
  //   Die Wahl der Tasten hier verhindern, dass S und R gleichzeitig bedient werden können.
endmodule

module D_FF__Pos__Neg__2_Flanken_getriggert (
  input  D,
  input  C,
  input  nEnable,
  output Q,
  output nQ
);

  wire not_1_out, Reset_out, Set_out;

  Pos_Neg_2_flankengetriggertes_D_FF pos_neg_2_flankengetriggertes_d_ff_1 (
    .D(D), .CP(C), .Reset(Reset_out), .Set(Set_out), .Enable(not_1_out), .Q(Q), .nQ(nQ));
  not not_1 (not_1_out, nEnable);
  Button Set (.out(Set_out));
  Button Reset (.out(Reset_out));

  // Notes on the sheet:
  //   D-FF, positiv-negativ 2-Flanken-getriggert
  //   Bemerkung:
  //   Auf steigende Vorderflanke (= positive Vorderflanke) wird der Wert von D detektiert und
  //   zwischengespeichert.
  //   Auf fallende Hinterflanke wird der zwischengespeicherte Wert an Q ausgegeben.
  //   Für C=0 oder C=1 geschieht nichts.
  //   ~Enable wurde tief aktiv gewählt, weil Logisim beim Aufstarten alle Eingänge tief setzt:
  //   Damit ist das D-FF sofort enabled.
  //   S und R wirken mit höchster Priorität, auch dann wenn das D-FF nicht enabled ist.
  //   Die Wahl der Tasten hier verhindern, dass S und R gleichzeitig bedient werden können.
endmodule

module D_FF__Neg__Pos__2_Flanken_getriggert (
  input  D,
  input  C,
  output Q,
  output nQ
);

  \Neg_Pos_2_flankengetriggertes_D_FF_ohne_Hilseingänge  \neg_pos_2_flankengetriggertes_d_ff_ohne_hilseingänge_1  (
    .D(D), .CP(C), .Q(Q), .nQ(nQ));

  // Notes on the sheet:
  //   D-FF, negativ-positiv 2-Flanken-getriggert
  //   Bemerkung:
  //   Auf fallende Vorderflanke (= negative Vorderflanke) wird der Wert von D detektiert und
  //   zwischengespeichert.
  //   Auf steigende Hinterflanke wird der zwischengespeicherte Wert an Q ausgegeben.
  //   Für C=0 oder C=1 geschieht nichts.
endmodule

module D_FF_erweitert__Neg__Pos__2_Flanken_getriggert (
  input  D,
  input  C,
  input  nEnable,
  output Q,
  output nQ
);

  wire not_1_out, Reset_out, Set_out;

  Neg_Pos_2_flankengetriggertes_D_FF neg_pos_2_flankengetriggertes_d_ff_1 (
    .D(D), .CP(C), .Reset(Reset_out), .Set(Set_out), .Enable(not_1_out), .Q(Q), .nQ(nQ));
  not not_1 (not_1_out, nEnable);
  Button Set (.out(Set_out));
  Button Reset (.out(Reset_out));

  // Notes on the sheet:
  //   D-FF, negativ-positiv 2-Flanken-getriggert
  //   Bemerkung:
  //   Auf fallende Vorderflanke (= negative Vorderflanke) wird der Wert von D detektiert und
  //   zwischengespeichert.
  //   Auf steigende Hinterflanke wird der zwischengespeicherte Wert an Q ausgegeben.
  //   Für C=0 oder C=1 geschieht nichts.
  //   ~Enable wurde tief aktiv gewählt, weil Logisim beim Aufstarten alle Eingänge tief setzt:
  //   Damit ist das D-FF sofort enabled.
  //   S und R wirken mit höchster Priorität, auch dann wenn das D-FF nicht enabled ist.
  //   Die Wahl der Tasten hier verhindern, dass S und R gleichzeitig bedient werden können.
endmodule

module JK_FF__Pos__1_Flanken_getriggert (
  input  J,
  input  C,
  input  K,
  output Q,
  output nQ
);

  \Positiv_1_flankengetriggertes_JK_FF_ohne_Hilfseingänge  \positiv_1_flankengetriggertes_jk_ff_ohne_hilfseingänge_1  (
    .J(J), .C(C), .K(K), .Q(Q), .nQ(nQ));

  // Notes on the sheet:
  //   JK-FF, positiv 1-Flanken-getriggert
  //   Bemerkung:
  //   Auf steigende Flanke (= positive Flanke) werden die Werte von J und K detektiert.
  //   Für J=K=0 bleibt Q unverändert.
  //   Für J=K=1 wird Q invertiert.
  //   Für J=0 und K=1 wird/bleibt Q=0.
  //   Für J=1 und K=0 wird/bleibt Q=1.
  //   Für C=0 oder C=1 oder auf die fallende Flanke (= negative Flanke) von C bleibt Q unverändert.
endmodule

module JK_FF_erweitert_Pos__1_Flanken_getriggert (
  input  J,
  input  C,
  input  K,
  input  nEnable,
  output Q,
  output nQ
);

  wire not_1_out, Reset_out, Set_out;

  Positiv_1_flankengetriggertes_JK_FF positiv_1_flankengetriggertes_jk_ff_1 (
    .J(J), .C(C), .K(K), .S(Set_out), .Enable(not_1_out), .R(Reset_out), .Q(Q), .nQ(nQ));
  not not_1 (not_1_out, nEnable);
  Button Set (.out(Set_out));
  Button Reset (.out(Reset_out));

  // Notes on the sheet:
  //   JK-FF, positiv 1-Flanken-getriggert
  //   Bemerkung:
  //   Auf steigende Flanke (= positive Flanke) werden die Werte von J und K detektiert.
  //   Für J=K=0 bleibt Q unverändert.
  //   Für J=K=1 wird Q invertiert.
  //   Für J=0 und K=1 wird/bleibt Q=0.
  //   Für J=1 und K=0 wird/bleibt Q=1.
  //   Für C=0 oder C=1 oder auf die fallende Flanke (= negative Flanke) von C bleibt Q unverändert.
  //   ~Enable wurde tief aktiv gewählt, weil Logisim beim Aufstarten alle Eingänge tief setzt:
  //   Damit ist das D-FF sofort enabled.
  //   S und R wirken mit höchster Priorität, auch dann wenn das D-FF nicht enabled ist.
  //   Die Wahl der Tasten hier verhindern, dass S und R gleichzeitig bedient werden können.
endmodule

module JK_FF__Pos__Neg__2_Flanken_getriggert (
  input  J,
  input  C,
  input  K,
  output Q,
  output nQ
);

  \Pos_Neg_2_flankengetriggertes_JK_FF_ohne_Hilfseingänge  \pos_neg_2_flankengetriggertes_jk_ff_ohne_hilfseingänge_1  (
    .J(J), .K(C), .CP(K), .Q(Q), .nQ(nQ));

  // Notes on the sheet:
  //   JK-FF, positiv-negativ 2-Flanken-getriggert
  //   Bemerkung:
  //   Auf steigende Vorderflanke (= positive Vorderflanke) werden die Werte von J und K detektiert.
  //   Für J=K=0 bleibt Zwischenspeicherung unverändert.
  //   Für J=K=1 wird Zwischenspeicherung invertiert.
  //   Für J=0 und K=1 wird/bleibt Zwischenspeicherung=0.
  //   Für J=1 und K=0 wird/bleibt Zwischenspeicherung=1.
  //   Auf fallende Hinterflanke wird der zwischengespeicherte Wert an Q ausgegeben.
  //   Für C=0 oder C=1 geschieht nichts.
endmodule

module JK_FF_erweitert__Pos__Neg__2_Flanken_getriggert (
  input  J,
  input  C,
  input  K,
  input  nEnable,
  output Q,
  output nQ
);

  wire not_1_out, Reset_out, Set_out;

  Pos_Neg_2_flankengetriggertes_JK_FF pos_neg_2_flankengetriggertes_jk_ff_1 (
    .J(J), .K(K), .CP(C), .Q(Q), .nQ(nQ), .Reset(Reset_out), .Set(Set_out), .Enable(not_1_out));
  not not_1 (not_1_out, nEnable);
  Button Set (.out(Set_out));
  Button Reset (.out(Reset_out));

  // Notes on the sheet:
  //   JK-FF, positiv-negativ 2-Flanken-getriggert
  //   Bemerkung:
  //   Auf steigende Vorderflanke (= positive Vorderflanke) werden die Werte von J und K detektiert.
  //   Für J=K=0 bleibt Zwischenspeicherung unverändert.
  //   Für J=K=1 wird Zwischenspeicherung invertiert.
  //   Für J=0 und K=1 wird/bleibt Zwischenspeicherung=0.
  //   Für J=1 und K=0 wird/bleibt Zwischenspeicherung=1.
  //   Auf fallende Hinterflanke wird der zwischengespeicherte Wert an Q ausgegeben.
  //   Für C=0 oder C=1 geschieht nichts.
  //   ~Enable wurde tief aktiv gewählt, weil Logisim beim Aufstarten alle Eingänge tief setzt:
  //   Damit ist das D-FF sofort enabled.
  //   S und R wirken mit höchster Priorität, auch dann wenn das D-FF nicht enabled ist.
  //   Die Wahl der Tasten hier verhindern, dass S und R gleichzeitig bedient werden können.
endmodule

module Sample_and_Hold__state_triggered (
  input  nEnable
);

  wire clock_1_out, Hold_out, zustandsgesteuertes_d_ff_aus_bibl_1_q, zustandsgesteuertes_d_ff_aus_bibl_2_q,
       zustandsgesteuertes_d_ff_aus_bibl_3_q, zustandsgesteuertes_d_ff_aus_bibl_4_q;
  wire [2:0] Controls;
  wire [3:0] counter_1_q;

  Counter #(.width(4), .max('hf)) counter_1 (.Q(counter_1_q), .clk(clock_1_out));  // open: load, D, count, carry, clr
  Clock clock_1 (.out(clock_1_out));
  Button Hold (.out(Hold_out));
  Button Reset (.out(Controls[0]));
  Button Set (.out(Controls[1]));
  not not_1 (Controls[2], nEnable);
  LED D3 (.in(counter_1_q[3]));
  LED D2 (.in(counter_1_q[2]));
  LED D1 (.in(counter_1_q[1]));
  LED D0 (.in(counter_1_q[0]));
  Zustandsgesteuertes_D_FF__aus_Bibl zustandsgesteuertes_d_ff_aus_bibl_1 (
    .C(Hold_out), .D(counter_1_q[3]), .S(Controls[1]), .Enable(Controls[2]), .R(Controls[0]),
    .Q(zustandsgesteuertes_d_ff_aus_bibl_1_q));  // open: nQ
  Zustandsgesteuertes_D_FF__aus_Bibl zustandsgesteuertes_d_ff_aus_bibl_2 (
    .C(Hold_out), .D(counter_1_q[2]), .S(Controls[1]), .Enable(Controls[2]), .R(Controls[0]),
    .Q(zustandsgesteuertes_d_ff_aus_bibl_2_q));  // open: nQ
  Zustandsgesteuertes_D_FF__aus_Bibl zustandsgesteuertes_d_ff_aus_bibl_3 (
    .C(Hold_out), .D(counter_1_q[1]), .S(Controls[1]), .Enable(Controls[2]), .R(Controls[0]),
    .Q(zustandsgesteuertes_d_ff_aus_bibl_3_q));  // open: nQ
  Zustandsgesteuertes_D_FF__aus_Bibl zustandsgesteuertes_d_ff_aus_bibl_4 (
    .C(Hold_out), .D(counter_1_q[0]), .S(Controls[1]), .Enable(Controls[2]), .R(Controls[0]),
    .Q(zustandsgesteuertes_d_ff_aus_bibl_4_q));  // open: nQ
  LED Q3 (.in(zustandsgesteuertes_d_ff_aus_bibl_1_q));
  LED Q2 (.in(zustandsgesteuertes_d_ff_aus_bibl_2_q));
  LED Q1 (.in(zustandsgesteuertes_d_ff_aus_bibl_3_q));
  LED Q0 (.in(zustandsgesteuertes_d_ff_aus_bibl_4_q));

  // Notes on the sheet:
  //   4-Bit Sample & Hold
  //   (Halten: Drücken und gedrückt halten)
endmodule

module Sample_and_Hold__edge_triggered (
  input  nEnable
);

  wire clock_1_out, Hold_out, positiv_1_flankengetriggertes_d_ff_1_q, positiv_1_flankengetriggertes_d_ff_2_q,
       positiv_1_flankengetriggertes_d_ff_3_q, positiv_1_flankengetriggertes_d_ff_4_q;
  wire [2:0] Controls;
  wire [3:0] counter_1_q;

  Counter #(.width(4), .max('hf)) counter_1 (.Q(counter_1_q), .clk(clock_1_out));  // open: load, D, count, carry, clr
  Clock clock_1 (.out(clock_1_out));
  onPosEdge onposedge_1 ();
  Button Hold (.out(Hold_out));
  Button Reset (.out(Controls[0]));
  Button Set (.out(Controls[1]));
  not not_1 (Controls[2], nEnable);
  LED D3 (.in(counter_1_q[3]));
  LED D2 (.in(counter_1_q[2]));
  LED D1 (.in(counter_1_q[1]));
  LED D0 (.in(counter_1_q[0]));
  Positiv_1_flankengetriggertes_D_FF positiv_1_flankengetriggertes_d_ff_1 (
    .Q(positiv_1_flankengetriggertes_d_ff_1_q), .C(Hold_out), .D(counter_1_q[3]), .S(Controls[1]),
    .R(Controls[0]), .Enable(Controls[2]));  // open: nQ
  Positiv_1_flankengetriggertes_D_FF positiv_1_flankengetriggertes_d_ff_2 (
    .Q(positiv_1_flankengetriggertes_d_ff_2_q), .C(Hold_out), .D(counter_1_q[2]), .S(Controls[1]),
    .R(Controls[0]), .Enable(Controls[2]));  // open: nQ
  Positiv_1_flankengetriggertes_D_FF positiv_1_flankengetriggertes_d_ff_3 (
    .Q(positiv_1_flankengetriggertes_d_ff_3_q), .C(Hold_out), .D(counter_1_q[1]), .S(Controls[1]),
    .R(Controls[0]), .Enable(Controls[2]));  // open: nQ
  Positiv_1_flankengetriggertes_D_FF positiv_1_flankengetriggertes_d_ff_4 (
    .Q(positiv_1_flankengetriggertes_d_ff_4_q), .C(Hold_out), .D(counter_1_q[0]), .S(Controls[1]),
    .R(Controls[0]), .Enable(Controls[2]));  // open: nQ
  LED Q3 (.in(positiv_1_flankengetriggertes_d_ff_1_q));
  LED Q2 (.in(positiv_1_flankengetriggertes_d_ff_2_q));
  LED Q1 (.in(positiv_1_flankengetriggertes_d_ff_3_q));
  LED Q0 (.in(positiv_1_flankengetriggertes_d_ff_4_q));

  // Notes on the sheet:
  //   4-Bit Hold
  //   (Ein- und Auslesen auf pos. Flanke)
endmodule

module Sample_and_Hold__double_edge_triggered (
  input  nEnable
);

  wire clock_1_out, Hold_out, pos_neg_2_flankengetriggertes_d_ff_1_q, pos_neg_2_flankengetriggertes_d_ff_2_q,
       pos_neg_2_flankengetriggertes_d_ff_3_q, pos_neg_2_flankengetriggertes_d_ff_4_q;
  wire [2:0] Controls;
  wire [3:0] counter_1_q;

  onPosThenNegEdge onposthennegedge_1 ();
  Counter #(.width(4), .max('hf)) counter_1 (.Q(counter_1_q), .clk(clock_1_out));  // open: load, D, count, carry, clr
  Clock clock_1 (.out(clock_1_out));
  Button Hold (.out(Hold_out));
  Button Reset (.out(Controls[0]));
  Button Set (.out(Controls[1]));
  not not_1 (Controls[2], nEnable);
  LED D3 (.in(counter_1_q[3]));
  LED D2 (.in(counter_1_q[2]));
  LED D1 (.in(counter_1_q[1]));
  LED D0 (.in(counter_1_q[0]));
  Pos_Neg_2_flankengetriggertes_D_FF pos_neg_2_flankengetriggertes_d_ff_1 (
    .D(counter_1_q[3]), .CP(Hold_out), .Reset(Controls[0]), .Set(Controls[1]), .Enable(Controls[2]),
    .Q(pos_neg_2_flankengetriggertes_d_ff_1_q));  // open: nQ
  Pos_Neg_2_flankengetriggertes_D_FF pos_neg_2_flankengetriggertes_d_ff_2 (
    .D(counter_1_q[2]), .CP(Hold_out), .Reset(Controls[0]), .Set(Controls[1]), .Enable(Controls[2]),
    .Q(pos_neg_2_flankengetriggertes_d_ff_2_q));  // open: nQ
  Pos_Neg_2_flankengetriggertes_D_FF pos_neg_2_flankengetriggertes_d_ff_3 (
    .D(counter_1_q[1]), .CP(Hold_out), .Reset(Controls[0]), .Set(Controls[1]), .Enable(Controls[2]),
    .Q(pos_neg_2_flankengetriggertes_d_ff_3_q));  // open: nQ
  Pos_Neg_2_flankengetriggertes_D_FF pos_neg_2_flankengetriggertes_d_ff_4 (
    .D(counter_1_q[0]), .CP(Hold_out), .Reset(Controls[0]), .Set(Controls[1]), .Enable(Controls[2]),
    .Q(pos_neg_2_flankengetriggertes_d_ff_4_q));  // open: nQ
  LED Q3 (.in(pos_neg_2_flankengetriggertes_d_ff_1_q));
  LED Q2 (.in(pos_neg_2_flankengetriggertes_d_ff_2_q));
  LED Q1 (.in(pos_neg_2_flankengetriggertes_d_ff_3_q));
  LED Q0 (.in(pos_neg_2_flankengetriggertes_d_ff_4_q));

  // Notes on the sheet:
  //   4-Bit Hold
  //   (Einlesen auf pos. Flanke)
  //   (Ausgeben auf neg. Flanke)
endmodule

module \Asynchroner_Modulo_8_Zähler  (
  input  R
);

  wire CP_out;
  wire [2:0] negativ_1_flankengetriggertes_jk_ff_1_q;

  Negativ_1_flankengetriggertes_JK_FF negativ_1_flankengetriggertes_jk_ff_1 (
    .J(1'b1), .C(CP_out), .K(1'b1), .S(1'b0), .Enable(1'b1), .R(R),
    .Q(negativ_1_flankengetriggertes_jk_ff_1_q[0]));  // open: nQ
  Clock CP (.out(CP_out));
  LED Q0_LSB (.in(negativ_1_flankengetriggertes_jk_ff_1_q[0]));
  Negativ_1_flankengetriggertes_JK_FF negativ_1_flankengetriggertes_jk_ff_2 (
    .J(1'b1), .C(negativ_1_flankengetriggertes_jk_ff_1_q[0]), .K(1'b1), .S(1'b0), .Enable(1'b1), .R(R),
    .Q(negativ_1_flankengetriggertes_jk_ff_1_q[1]));  // open: nQ
  LED Q1 (.in(negativ_1_flankengetriggertes_jk_ff_1_q[1]));
  Negativ_1_flankengetriggertes_JK_FF negativ_1_flankengetriggertes_jk_ff_3 (
    .J(1'b1), .C(negativ_1_flankengetriggertes_jk_ff_1_q[1]), .K(1'b1), .S(1'b0), .Enable(1'b1), .R(R),
    .Q(negativ_1_flankengetriggertes_jk_ff_1_q[2]));  // open: nQ
  LED Q2_MSB (.in(negativ_1_flankengetriggertes_jk_ff_1_q[2]));
  Hex_Digit_Display hex_digit_display_1 (.value({1'b0, negativ_1_flankengetriggertes_jk_ff_1_q}));  // open: dp

  // Notes on the sheet:
  //   Asynchroner Modulo-8-Zähler (vorwärts)
endmodule

module \Asynchroner_Modulo_10_Zähler  (
);

  wire and_1_out, CP_out;
  wire [3:0] negativ_1_flankengetriggertes_jk_ff_1_q;

  Negativ_1_flankengetriggertes_JK_FF negativ_1_flankengetriggertes_jk_ff_1 (
    .J(1'b1), .C(CP_out), .K(1'b1), .S(1'b0), .Enable(1'b1), .R(and_1_out),
    .Q(negativ_1_flankengetriggertes_jk_ff_1_q[0]));  // open: nQ
  Clock CP (.out(CP_out));
  and and_1 (and_1_out, negativ_1_flankengetriggertes_jk_ff_1_q[3], negativ_1_flankengetriggertes_jk_ff_1_q[1]);
  Negativ_1_flankengetriggertes_JK_FF negativ_1_flankengetriggertes_jk_ff_2 (
    .J(1'b1), .C(negativ_1_flankengetriggertes_jk_ff_1_q[0]), .K(1'b1), .S(1'b0), .Enable(1'b1),
    .R(and_1_out), .Q(negativ_1_flankengetriggertes_jk_ff_1_q[1]));  // open: nQ
  Arrow arrow_1 ();
  LED Q0_LSB (.in(negativ_1_flankengetriggertes_jk_ff_1_q[0]));
  Negativ_1_flankengetriggertes_JK_FF negativ_1_flankengetriggertes_jk_ff_3 (
    .J(1'b1), .C(negativ_1_flankengetriggertes_jk_ff_1_q[1]), .K(1'b1), .S(1'b0), .Enable(1'b1),
    .R(and_1_out), .Q(negativ_1_flankengetriggertes_jk_ff_1_q[2]));  // open: nQ
  LED Q1 (.in(negativ_1_flankengetriggertes_jk_ff_1_q[1]));
  Arrow arrow_2 ();
  Negativ_1_flankengetriggertes_JK_FF negativ_1_flankengetriggertes_jk_ff_4 (
    .J(1'b1), .C(negativ_1_flankengetriggertes_jk_ff_1_q[2]), .K(1'b1), .S(1'b0), .Enable(1'b1),
    .R(and_1_out), .Q(negativ_1_flankengetriggertes_jk_ff_1_q[3]));  // open: nQ
  LED Q2 (.in(negativ_1_flankengetriggertes_jk_ff_1_q[2]));
  LED Q3_MSB (.in(negativ_1_flankengetriggertes_jk_ff_1_q[3]));
  Hex_Digit_Display hex_digit_display_1 (.value(negativ_1_flankengetriggertes_jk_ff_1_q));  // open: dp

  // Notes on the sheet:
  //   Asynchroner Modulo-10-Zähler (vorwärts)
endmodule

module Delay_Box (
  input  in_1,
  output out_2
);


  assign out_2 = in_1;
endmodule

module onPosEdge (
);


  // Notes on the sheet:
  //   Positive Edge Symbol in Design View
endmodule

module onPosThenNegEdge (
);


  // Notes on the sheet:
  //   Positive and Negative Edge Symbol in Design View
endmodule

module RS_FF__aus_Bibliothek (
  input  S,
  input  R,
  output Q,
  output nQ
);

  S_R_Flip_Flop #(.trigger("low")) s_r_ff_1 (
    .S(1'b0), .clk(1'b0), .R(1'b0), .Q(Q), .Qn(nQ), .preset(S), .reset(R), .en(1'b1));
endmodule

module Zustandsgesteuertes_D_FF__Eigenbau (
  input  D,
  input  C,
  input  D_2,
  input  C_2,
  output Q,
  output nQ,
  output Q_2,
  output nQ_2
);

  wire nand_1_out, nand_2_out;

  nand nand_1 (nand_1_out, D, C);
  nand nand_2 (nand_2_out, nand_1_out, C);
  Multiplexer #(.enable("false")) multiplexer_1 (.in0(Q_2), .in1(D_2), .out(Q_2), .sel(C_2));
  nand nand_3 (Q, nand_1_out, nQ);
  nand nand_4 (nQ, Q, nand_2_out);
  not not_1 (nQ_2, Q_2);

  // Notes on the sheet:
  //   Latch mit Nand realisiert
  //   Data
  //   ~EnableLatching
  //   Latch mit MUX realisiert
  //   Data
  //   ~EnableLatching
  //   Zustandsgesteuertes D-FF
  //   (D für Delay)
  //   Bemerkung:
  //   Logisim tut sich schwer mit Rückkopplungen,
  //   daher bei Error-Meldungen vorerst C zwei-
  //   mal betätigen (on - off)
endmodule

module Zustandsgesteuertes_D_FF_reduziert__aus_Bibl (
  input  C,
  input  D,
  output Q,
  output nQ
);

  D_Flip_Flop #(.trigger("high")) d_ff_1 (.clk(C), .D(D), .Q(Q), .Qn(nQ), .preset(1'b0), .en(1'b1), .reset(1'b0));

  // Notes on the sheet:
  //   D-FF aus Logisim-Bibliothek (Property: H-Niveau)
endmodule

module Zustandsgesteuertes_D_FF__aus_Bibl (
  input  C,
  input  D,
  input  S,
  input  Enable,
  input  R,
  output Q,
  output nQ
);

  wire not_1_out;

  not not_1 (not_1_out, C);
  D_Flip_Flop #(.trigger("low")) d_ff_1 (.clk(not_1_out), .D(D), .Q(Q), .Qn(nQ), .preset(S), .en(Enable), .reset(R));

  // Notes on the sheet:
  //   D-FF aus Logisim-Bibliothek (Property: L-Niveau)
endmodule

module \Positiv_1_flankengetriggertes_D_FF_ohne_Hilfseingänge  (
  input  C,
  input  D,
  output Q,
  output nQ
);

  D_Flip_Flop d_ff_1 (.clk(C), .D(D), .Q(Q), .Qn(nQ), .preset(1'b0), .en(1'b1), .reset(1'b0));

  // Notes on the sheet:
  //   D-FF aus Logisim-Bibliothek (Property: Steigende Flanke)
endmodule

module Positiv_1_flankengetriggertes_D_FF (
  input  C,
  input  D,
  input  S,
  input  Enable,
  input  R,
  output Q,
  output nQ
);

  D_Flip_Flop d_ff_1 (.clk(C), .D(D), .Q(Q), .Qn(nQ), .preset(S), .en(Enable), .reset(R));

  // Notes on the sheet:
  //   D-FF aus Logisim-Bibliothek (Property: Steigende Flanke)
endmodule

module Negativ_1_flankengetriggertes_D_FF (
  input  C,
  input  D,
  input  S,
  input  Enable,
  input  R,
  output Q,
  output nQ
);

  D_Flip_Flop #(.trigger("falling")) d_ff_1 (.clk(C), .D(D), .Q(Q), .Qn(nQ), .preset(S), .en(Enable), .reset(R));

  // Notes on the sheet:
  //   D-FF aus Logisim-Bibliothek (Property: Fallende Flanke)
endmodule

module Pos_Neg_2_flankengetriggertes_D_FF (
  input  D,
  input  CP,
  input  Reset,
  input  Set,
  input  Enable,
  output Q,
  output nQ
);

  wire not_1_out, positiv_1_flankengetriggertes_d_ff_1_q;

  Positiv_1_flankengetriggertes_D_FF positiv_1_flankengetriggertes_d_ff_1 (
    .Q(positiv_1_flankengetriggertes_d_ff_1_q), .C(CP), .D(D), .S(Set), .R(Reset), .Enable(Enable));  // open: nQ
  not not_1 (not_1_out, CP);
  Positiv_1_flankengetriggertes_D_FF positiv_1_flankengetriggertes_d_ff_2 (
    .Q(Q), .C(not_1_out), .D(positiv_1_flankengetriggertes_d_ff_1_q), .S(Set), .R(Reset), .Enable(Enable),
    .nQ(nQ));

  // Notes on the sheet:
  //   Master-Slave D-FF
endmodule

module \Neg_Pos_2_flankengetriggertes_D_FF_ohne_Hilseingänge  (
  input  D,
  input  CP,
  output Q,
  output nQ
);

  wire not_1_out, positiv_1_flankengetriggertes_d_ff_1_q;

  Positiv_1_flankengetriggertes_D_FF positiv_1_flankengetriggertes_d_ff_1 (
    .Q(positiv_1_flankengetriggertes_d_ff_1_q), .C(not_1_out), .D(D), .S(1'b0), .R(1'b0), .Enable(1'b1));  // open: nQ
  not not_1 (not_1_out, CP);
  Positiv_1_flankengetriggertes_D_FF positiv_1_flankengetriggertes_d_ff_2 (
    .Q(Q), .C(CP), .D(positiv_1_flankengetriggertes_d_ff_1_q), .S(1'b0), .R(1'b0), .Enable(1'b1), .nQ(nQ));

  // Notes on the sheet:
  //   Master-Slave D-FF
endmodule

module Neg_Pos_2_flankengetriggertes_D_FF (
  input  D,
  input  CP,
  input  Reset,
  input  Set,
  input  Enable,
  output Q,
  output nQ
);

  wire not_1_out, positiv_1_flankengetriggertes_d_ff_1_q;

  Positiv_1_flankengetriggertes_D_FF positiv_1_flankengetriggertes_d_ff_1 (
    .Q(positiv_1_flankengetriggertes_d_ff_1_q), .C(not_1_out), .D(D), .S(Set), .R(Reset), .Enable(Enable));  // open: nQ
  not not_1 (not_1_out, CP);
  Positiv_1_flankengetriggertes_D_FF positiv_1_flankengetriggertes_d_ff_2 (
    .Q(Q), .C(CP), .D(positiv_1_flankengetriggertes_d_ff_1_q), .S(Set), .R(Reset), .Enable(Enable), .nQ(nQ));

  // Notes on the sheet:
  //   Master-Slave D-FF
endmodule

module \Positiv_1_flankengetriggertes_JK_FF_ohne_Hilfseingänge  (
  input  J,
  input  C,
  input  K,
  output Q,
  output nQ
);

  J_K_Flip_Flop j_k_ff_1 (.J(J), .clk(C), .K(K), .Q(Q), .Qn(nQ), .preset(1'b0), .en(1'b1), .reset(1'b0));

  // Notes on the sheet:
  //   JK-FF aus Logisim-Bibliothek (Property: Steigende Flanke)
endmodule

module Positiv_1_flankengetriggertes_JK_FF (
  input  J,
  input  C,
  input  K,
  input  S,
  input  Enable,
  input  R,
  output Q,
  output nQ
);

  J_K_Flip_Flop j_k_ff_1 (.J(J), .clk(C), .K(K), .Q(Q), .Qn(nQ), .preset(S), .en(Enable), .reset(R));

  // Notes on the sheet:
  //   JK-FF aus Logisim-Bibliothek (Property: Steigende Flanke)
endmodule

module Negativ_1_flankengetriggertes_JK_FF (
  input  J,
  input  C,
  input  K,
  input  S,
  input  Enable,
  input  R,
  output Q,
  output nQ
);

  J_K_Flip_Flop #(.trigger("falling")) j_k_ff_1 (
    .J(J), .clk(C), .K(K), .Q(Q), .Qn(nQ), .preset(S), .en(Enable), .reset(R));

  // Notes on the sheet:
  //   JK-FF aus Logisim-Bibliothek (Property: Fallende Flanke)
endmodule

module \Pos_Neg_2_flankengetriggertes_JK_FF_ohne_Hilfseingänge  (
  input  J,
  input  K,
  input  CP,
  output Q,
  output nQ
);

  wire not_1_out, positiv_1_flankengetriggertes_jk_ff_1_q;

  Positiv_1_flankengetriggertes_JK_FF positiv_1_flankengetriggertes_jk_ff_1 (
    .J(J), .C(CP), .K(K), .S(1'b0), .Enable(1'b1), .R(1'b0), .Q(positiv_1_flankengetriggertes_jk_ff_1_q));  // open: nQ
  not not_1 (not_1_out, CP);
  Positiv_1_flankengetriggertes_D_FF positiv_1_flankengetriggertes_d_ff_1 (
    .Q(Q), .C(not_1_out), .D(positiv_1_flankengetriggertes_jk_ff_1_q), .S(1'b0), .R(1'b0), .Enable(1'b1),
    .nQ(nQ));

  // Notes on the sheet:
  //   Master-Slave JK-FF
endmodule

module Pos_Neg_2_flankengetriggertes_JK_FF (
  input  J,
  input  K,
  input  CP,
  input  Reset,
  input  Set,
  input  Enable,
  output Q,
  output nQ
);

  wire not_1_out, positiv_1_flankengetriggertes_jk_ff_1_q;

  Positiv_1_flankengetriggertes_JK_FF positiv_1_flankengetriggertes_jk_ff_1 (
    .J(J), .C(CP), .K(K), .S(Set), .Enable(Enable), .R(Reset), .Q(positiv_1_flankengetriggertes_jk_ff_1_q));  // open: nQ
  not not_1 (not_1_out, CP);
  Positiv_1_flankengetriggertes_D_FF positiv_1_flankengetriggertes_d_ff_1 (
    .Q(Q), .C(not_1_out), .D(positiv_1_flankengetriggertes_jk_ff_1_q), .S(Set), .R(Reset), .Enable(Enable),
    .nQ(nQ));

  // Notes on the sheet:
  //   Master-Slave JK-FF
endmodule
