// Logisim project schaltwerke - synchrone schaltwerke.circ as structural Verilog
module Verkehrsampel_1 (
);

  wire and_1_out, CP_out, d_ff_mirrored_1_q, d_ff_mirrored_2_q, d_ff_mirrored_3_q, not_1_out, xor_1_out;

  onPosEdge onposedge_1 ();
  Button CP (.out(CP_out));
  Arrow arrow_1 ();
  Arrow arrow_2 ();
  Arrow arrow_3 ();
  D_FF_mirrored d_ff_mirrored_1 (
    .C(CP_out), .D(xor_1_out), .S(1'b0), .Enable(1'b1), .R(1'b0), .Q(d_ff_mirrored_1_q));  // open: nQ
  D_FF_mirrored d_ff_mirrored_2 (
    .C(CP_out), .D(not_1_out), .S(1'b0), .Enable(1'b1), .R(1'b0), .Q(d_ff_mirrored_2_q));  // open: nQ
  D_FF_mirrored d_ff_mirrored_3 (
    .C(CP_out), .D(and_1_out), .S(1'b0), .Enable(1'b1), .R(1'b0), .Q(d_ff_mirrored_3_q));  // open: nQ
  and and_1 (and_1_out, d_ff_mirrored_1_q, d_ff_mirrored_2_q);
  not not_1 (not_1_out, d_ff_mirrored_2_q);
  xor xor_1 (xor_1_out, d_ff_mirrored_2_q, d_ff_mirrored_1_q);
  Arrow arrow_4 ();
  Arrow arrow_5 ();
  Arrow arrow_6 ();
  Arrow arrow_7 ();
  Arrow arrow_8 ();
  Arrow arrow_9 ();
  LED y2 (.in(d_ff_mirrored_1_q));
  LED y1 (.in(d_ff_mirrored_2_q));
  LED y0 (.in(d_ff_mirrored_3_q));

  // Notes on the sheet:
  //   z2
  //   t
  //   z1
  //   t
  //   z0
  //   t
  //   z2
  //   z1
  //   z0
  //   t+1
  //   t+1
  //   t+1
endmodule

module Verkehrsampel_2 (
);

  wire CP_out, memory_1_z0_t, memory_1_z1_t, memory_1_z2_t, sn1_1_z0_t_1, sn1_1_z1_t_1, sn1_1_z2_t_1;

  onPosEdge onposedge_1 ();
  Button CP (.out(CP_out));
  SN1 sn1_1 (
    .z0_t_1(sn1_1_z0_t_1), .z1_t(memory_1_z1_t), .z1_t_1(sn1_1_z1_t_1), .z2_t(memory_1_z2_t),
    .z2_t_1(sn1_1_z2_t_1));  // open: z0_t
  Arrow arrow_1 ();
  Arrow arrow_2 ();
  Arrow arrow_3 ();
  Memory memory_1 (
    .Controls(3'b100), .z2_t(memory_1_z2_t), .z1_t(memory_1_z1_t), .z0_t(memory_1_z0_t), .CP(CP_out),
    .z2_t_1(sn1_1_z2_t_1), .z1_t_1(sn1_1_z1_t_1), .z0_t_1(sn1_1_z0_t_1));
  Arrow arrow_4 ();
  Arrow arrow_5 ();
  Arrow arrow_6 ();
  Arrow arrow_7 ();
  LED y2 (.in(memory_1_z2_t));
  LED y1 (.in(memory_1_z1_t));
  LED y0 (.in(memory_1_z0_t));
endmodule

module Verkehrsampel_3 (
  input  Enable
);

  wire CP_out, memory_1_z0_t, memory_1_z1_t, memory_1_z2_t, sn1_1_z0_t_1, sn1_1_z1_t_1, sn1_1_z2_t_1,
       sn2_1_y0, sn2_1_y1, sn2_1_y2;
  wire [1:0] Controls;

  onPosEdge onposedge_1 ();
  Button CP (.out(CP_out));
  Button Reset (.out(Controls[0]));
  Button Set (.out(Controls[1]));
  SN1 sn1_1 (
    .z0_t(memory_1_z0_t), .z0_t_1(sn1_1_z0_t_1), .z1_t(memory_1_z1_t), .z1_t_1(sn1_1_z1_t_1),
    .z2_t(memory_1_z2_t), .z2_t_1(sn1_1_z2_t_1));
  Arrow arrow_1 ();
  Arrow arrow_2 ();
  Arrow arrow_3 ();
  Memory memory_1 (
    .Controls({Enable, Controls}), .z2_t(memory_1_z2_t), .z1_t(memory_1_z1_t), .z0_t(memory_1_z0_t),
    .CP(CP_out), .z2_t_1(sn1_1_z2_t_1), .z1_t_1(sn1_1_z1_t_1), .z0_t_1(sn1_1_z0_t_1));
  SN2 sn2_1 (
    .z2_t(memory_1_z2_t), .y2(sn2_1_y2), .z1_t(memory_1_z1_t), .y1(sn2_1_y1), .z0_t(memory_1_z0_t),
    .y0(sn2_1_y0));
  Arrow arrow_4 ();
  Arrow arrow_5 ();
  Arrow arrow_6 ();
  Arrow arrow_7 ();
  LED y2 (.in(sn2_1_y2));
  LED y1 (.in(sn2_1_y1));
  LED y0 (.in(sn2_1_y0));

  // Other names for the same wires on the sheet: Controls[2] = Enable
endmodule

module Schieberegister__Serie__Parallelregister (
  input  INSR,
  input  A,
  input  B,
  input  C,
  input  D,
  input  INSL,
  input  S1,
  input  S0,
  input  CP,
  input  nR
);

  wire and_1_out, and_2_out, and_3_out, and_4_out, and_5_out, and_6_out, and_7_out, and_8_out, and_9_out,
       and_10_out, and_11_out, and_12_out, and_13_out, d_ff_1_q, d_ff_2_q, d_ff_3_q, d_ff_4_q, nor_1_out,
       nor_2_out, not_1_out, not_2_out, not_3_out, not_4_out, or_1_out, or_2_out, or_3_out, or_4_out;

  onPosEdge onposedge_1 ();
  not not_1 (not_1_out, S1);
  not not_2 (not_2_out, S0);
  not not_3 (not_3_out, CP);
  not not_4 (not_4_out, nR);
  and and_1 (and_1_out, not_1_out, not_2_out);
  nor nor_1 (nor_1_out, not_1_out, not_2_out);
  and and_2 (and_2_out, INSR, not_2_out);
  nor nor_2 (nor_2_out, and_1_out, not_3_out);
  and and_3 (and_3_out, not_1_out, d_ff_2_q);
  and and_4 (and_4_out, nor_1_out, A);
  or or_1 (or_1_out, and_2_out, and_4_out, and_3_out);
  D_FF d_ff_1 (.Q(d_ff_1_q), .C(nor_2_out), .D(or_1_out), .R(not_4_out), .Enable(1'b1));  // open: S, nQ
  and and_5 (and_5_out, d_ff_1_q, not_2_out);
  LED QA (.in(d_ff_1_q));
  and and_6 (and_6_out, nor_1_out, B);
  and and_7 (and_7_out, not_1_out, d_ff_3_q);
  or or_2 (or_2_out, and_5_out, and_6_out, and_7_out);
  D_FF d_ff_2 (.Q(d_ff_2_q), .C(nor_2_out), .D(or_2_out), .R(not_4_out), .Enable(1'b1));  // open: S, nQ
  LED QB (.in(d_ff_2_q));
  and and_8 (and_8_out, d_ff_2_q, not_2_out);
  and and_9 (and_9_out, nor_1_out, C);
  or or_3 (or_3_out, and_8_out, and_9_out, and_10_out);
  and and_10 (and_10_out, not_1_out, d_ff_4_q);
  D_FF d_ff_3 (.Q(d_ff_3_q), .C(nor_2_out), .D(or_3_out), .R(not_4_out), .Enable(1'b1));  // open: S, nQ
  and and_11 (and_11_out, d_ff_3_q, not_2_out);
  LED QC (.in(d_ff_3_q));
  and and_12 (and_12_out, not_1_out, INSL);
  and and_13 (and_13_out, nor_1_out, D);
  or or_4 (or_4_out, and_11_out, and_13_out, and_12_out);
  D_FF d_ff_4 (.Q(d_ff_4_q), .C(nor_2_out), .D(or_4_out), .R(not_4_out), .Enable(1'b1));  // open: S, nQ
  LED QD (.in(d_ff_4_q));
endmodule

module \Modulo_6__Zähler  (
  input  CP
);

  wire and_1_out, d_ff_neg_1_nq, d_ff_neg_1_q, d_ff_neg_2_nq, d_ff_neg_2_q, d_ff_neg_3_nq, d_ff_neg_3_q,
       nand_1_out, not_1_out, or_1_out, or_2_out, or_3_out;

  onPosEdge onposedge_1 ();
  line line_1 ();
  line line_2 ();
  line line_3 ();
  line line_4 ();
  not not_1 (not_1_out, CP);
  or or_1 (or_1_out, d_ff_neg_3_nq, d_ff_neg_2_nq);
  D_FF_neg d_ff_neg_1 (
    .C(not_1_out), .D(or_1_out), .S(1'b0), .Enable(1'b1), .R(1'b0), .Q(d_ff_neg_1_q), .nQ(d_ff_neg_1_nq));
  line line_5 ();
  line line_6 ();
  LED Q2__MSB (.in(d_ff_neg_1_q));
  or or_2 (or_2_out, d_ff_neg_3_nq, d_ff_neg_2_q);
  and and_1 (and_1_out, d_ff_neg_1_q, or_2_out);
  line line_7 ();
  line line_8 ();
  D_FF_neg d_ff_neg_2 (
    .C(not_1_out), .D(and_1_out), .S(1'b0), .Enable(1'b1), .R(1'b0), .Q(d_ff_neg_2_q), .nQ(d_ff_neg_2_nq));
  LED Q1 (.in(d_ff_neg_2_q));
  line line_9 ();
  or or_3 (or_3_out, d_ff_neg_2_q, d_ff_neg_1_nq);
  line line_10 ();
  D_FF_neg d_ff_neg_3 (
    .C(not_1_out), .D(or_3_out), .S(1'b0), .Enable(1'b1), .R(1'b0), .Q(d_ff_neg_3_q), .nQ(d_ff_neg_3_nq));
  LED Q0 (.in(d_ff_neg_3_q));
  line line_11 ();
  line line_12 ();
  LED nW (.in(nand_1_out));
  nand nand_1 (nand_1_out, d_ff_neg_2_q, d_ff_neg_1_q, d_ff_neg_3_q);

  // Notes on the sheet:
  //   SN1
endmodule

module Memory (
  input  z2_t_1,
  input  [2:0] Controls,
  input  z1_t_1,
  input  z0_t_1,
  input  CP,
  output z2_t,
  output z1_t,
  output z0_t
);

  Arrow arrow_1 ();
  D_FF_mirrored d_ff_mirrored_1 (
    .C(CP), .D(z2_t_1), .S(Controls[1]), .Enable(Controls[2]), .R(Controls[0]), .Q(z2_t));  // open: nQ
  D_FF_mirrored d_ff_mirrored_2 (
    .C(CP), .D(z1_t_1), .S(Controls[1]), .Enable(Controls[2]), .R(Controls[0]), .Q(z1_t));  // open: nQ
  D_FF_mirrored d_ff_mirrored_3 (
    .C(CP), .D(z0_t_1), .S(Controls[1]), .Enable(Controls[2]), .R(Controls[0]), .Q(z0_t));  // open: nQ
  Arrow arrow_2 ();
  Arrow arrow_3 ();
  Arrow arrow_4 ();
  Arrow arrow_5 ();
  Arrow arrow_6 ();
  Arrow arrow_7 ();
endmodule

module SN1 (
  input  z2_t,
  input  z1_t,
  input  z0_t,
  output z2_t_1,
  output z1_t_1,
  output z0_t_1
);

  not not_1 (z1_t_1, z1_t);
  xor xor_1 (z2_t_1, z2_t, z1_t);
  and and_1 (z0_t_1, z2_t, z1_t);
endmodule

module SN2 (
  input  z2_t,
  input  z1_t,
  input  z0_t,
  output y2,
  output y1,
  output y0
);


  assign y0 = z0_t;
  assign y1 = z1_t;
  assign y2 = z2_t;
endmodule

module D_FF (
  input  C,
  input  D,
  input  S,
  input  Enable,
  input  R,
  output Q,
  output nQ
);

  D_Flip_Flop d_ff_1 (.clk(C), .D(D), .Q(Q), .Qn(nQ), .preset(S), .en(Enable), .reset(R));
endmodule

module D_FF_mirrored (
  input  C,
  input  D,
  input  S,
  input  Enable,
  input  R,
  output Q,
  output nQ
);

  D_Flip_Flop d_ff_1 (.clk(C), .D(D), .Q(Q), .Qn(nQ), .preset(S), .en(Enable), .reset(R));
endmodule

module line (
);


  // Notes on the sheet:
  //   line in design view
endmodule

module D_FF_neg (
  input  C,
  input  D,
  input  S,
  input  Enable,
  input  R,
  output Q,
  output nQ
);

  D_Flip_Flop #(.trigger("falling")) d_ff_1 (.clk(C), .D(D), .Q(Q), .Qn(nQ), .preset(S), .en(Enable), .reset(R));
endmodule
